// Logisim project 2c.circ as structural Verilog: 1 circuit, main circuit main
module main (
  input  [7:0] in_1,
  input  L_H,
  input  ENABLE,
  input  CLK,
  input  [1:0] Function_Selector,
  output [15:0] out_6
);

  wire and_1_out, and_2_out, and_3_out, and_4_out, and_5_out, and_6_out, and_7_out, and_8_out, and_9_out,
       and_10_out, and_11_out, and_12_out, and_13_out, and_14_out, and_15_out, and_16_out,
       Funsel_selector_out, multiplexer_1_out, multiplexer_2_out, multiplexer_3_out, multiplexer_4_out,
       multiplexer_5_out, multiplexer_6_out, multiplexer_7_out, multiplexer_8_out, multiplexer_9_out,
       multiplexer_10_out, multiplexer_11_out, multiplexer_12_out, multiplexer_13_out, multiplexer_14_out,
       multiplexer_15_out, multiplexer_16_out, multiplexer_17_out, multiplexer_18_out, nor_1_out, nor_2_out,
       nor_3_out, nor_4_out, nor_5_out, nor_6_out, nor_7_out, nor_8_out, nor_9_out, nor_10_out, nor_11_out,
       nor_12_out, nor_13_out, nor_14_out, not_1_out, not_2_out, not_3_out, not_4_out, not_5_out, not_6_out,
       not_7_out, not_8_out, not_9_out, not_10_out, not_11_out, xor_1_out, xor_2_out, xor_3_out, xor_4_out,
       xor_5_out, xor_6_out, xor_7_out, xor_8_out, xor_9_out, xor_10_out, xor_11_out, xor_12_out, xor_13_out,
       xor_14_out, xor_15_out, xor_16_out, xor_17_out, xor_18_out, xor_19_out, xor_20_out, xor_21_out,
       xor_22_out, xor_23_out, xor_24_out, xor_25_out, xor_26_out, xor_27_out, xor_28_out, xor_29_out,
       xor_30_out;

  Hex_Digit_Display hex_digit_display_1 (.value(in_1[7:4]));  // open: dp
  Hex_Digit_Display hex_digit_display_2 (.value(in_1[3:0]));  // open: dp
  not not_1 (not_1_out, nor_1_out);
  not not_2 (not_2_out, nor_2_out);
  not not_3 (not_3_out, nor_3_out);
  not not_4 (not_4_out, nor_4_out);
  not not_5 (not_5_out, nor_5_out);
  not not_6 (not_6_out, nor_6_out);
  not not_7 (not_7_out, nor_7_out);
  and Funsel_selector (Funsel_selector_out, Function_Selector[1], Function_Selector[0]);
  and and_1 (and_1_out, and_9_out, out_6[7]);
  nor nor_1 (nor_1_out, not_9_out, out_6[7]);
  and and_2 (and_2_out, and_1_out, out_6[8]);
  nor nor_2 (nor_2_out, not_1_out, out_6[8]);
  and and_3 (and_3_out, and_2_out, out_6[9]);
  nor nor_3 (nor_3_out, not_2_out, out_6[9]);
  and and_4 (and_4_out, and_3_out, out_6[10]);
  nor nor_4 (nor_4_out, not_3_out, out_6[10]);
  and and_5 (and_5_out, and_4_out, out_6[11]);
  nor nor_5 (nor_5_out, not_4_out, out_6[11]);
  and and_6 (and_6_out, and_5_out, out_6[12]);
  nor nor_6 (nor_6_out, not_5_out, out_6[12]);
  and and_7 (and_7_out, and_6_out, out_6[13]);
  nor nor_7 (nor_7_out, out_6[13], not_6_out);
  and and_8 (and_8_out, and_7_out, out_6[14]);
  and and_9 (and_9_out, out_6[0], out_6[1], out_6[2], out_6[6], out_6[3], out_6[4], out_6[5]);
  nor nor_8 (nor_8_out, out_6[14], not_7_out);
  xor xor_1 (xor_1_out, out_6[0], out_6[1]);
  not not_8 (not_8_out, out_6[0]);
  xor xor_2 (xor_2_out, not_8_out, out_6[1]);
  and and_10 (and_10_out, out_6[0], out_6[1]);
  and and_11 (and_11_out, out_6[0], out_6[2], out_6[1]);
  and and_12 (and_12_out, out_6[0], out_6[1], out_6[2], out_6[3]);
  and and_13 (and_13_out, out_6[0], out_6[1], out_6[2], out_6[3], out_6[4]);
  and and_14 (and_14_out, out_6[0], out_6[1], out_6[2], out_6[3], out_6[4], out_6[5]);
  nor nor_9 (nor_9_out, out_6[0], out_6[1], out_6[2], out_6[6], out_6[3], out_6[4], out_6[5]);
  not not_9 (not_9_out, nor_9_out);
  not not_10 (not_10_out, L_H);
  xor xor_3 (xor_3_out, and_1_out, out_6[8]);
  xor xor_4 (xor_4_out, nor_1_out, out_6[8]);
  xor xor_5 (xor_5_out, and_2_out, out_6[9]);
  xor xor_6 (xor_6_out, out_6[9], nor_2_out);
  xor xor_7 (xor_7_out, and_3_out, out_6[10]);
  xor xor_8 (xor_8_out, out_6[10], nor_3_out);
  xor xor_9 (xor_9_out, and_4_out, out_6[11]);
  xor xor_10 (xor_10_out, out_6[11], nor_4_out);
  xor xor_11 (xor_11_out, and_5_out, out_6[12]);
  xor xor_12 (xor_12_out, out_6[12], nor_5_out);
  xor xor_13 (xor_13_out, and_6_out, out_6[13]);
  xor xor_14 (xor_14_out, out_6[13], nor_6_out);
  xor xor_15 (xor_15_out, and_7_out, out_6[14]);
  xor xor_16 (xor_16_out, out_6[14], nor_7_out);
  xor xor_17 (xor_17_out, and_8_out, out_6[15]);
  xor xor_18 (xor_18_out, and_10_out, out_6[2]);
  nor nor_10 (nor_10_out, out_6[0], out_6[1]);
  xor xor_19 (xor_19_out, nor_10_out, out_6[2]);
  xor xor_20 (xor_20_out, and_11_out, out_6[3]);
  nor nor_11 (nor_11_out, out_6[0], out_6[2], out_6[1]);
  xor xor_21 (xor_21_out, nor_11_out, out_6[3]);
  xor xor_22 (xor_22_out, and_12_out, out_6[4]);
  xor xor_23 (xor_23_out, nor_12_out, out_6[4]);
  nor nor_12 (nor_12_out, out_6[0], out_6[1], out_6[2], out_6[3]);
  xor xor_24 (xor_24_out, and_13_out, out_6[5]);
  nor nor_13 (nor_13_out, out_6[3], out_6[0], out_6[1], out_6[2], out_6[4]);
  xor xor_25 (xor_25_out, nor_13_out, out_6[5]);
  xor xor_26 (xor_26_out, and_14_out, out_6[6]);
  nor nor_14 (nor_14_out, out_6[0], out_6[1], out_6[2], out_6[3], out_6[4], out_6[5]);
  xor xor_27 (xor_27_out, nor_14_out, out_6[6]);
  xor xor_28 (xor_28_out, and_9_out, out_6[7]);
  xor xor_29 (xor_29_out, nor_9_out, out_6[7]);
  Multiplexer multiplexer_1 (
    .in0(ENABLE), .in1(not_10_out), .out(multiplexer_1_out), .sel(Funsel_selector_out));  // open: en
  xor xor_30 (xor_30_out, nor_8_out, out_6[15]);
  Multiplexer multiplexer_2 (.in0(ENABLE), .in1(L_H), .out(multiplexer_2_out), .sel(Funsel_selector_out));  // open: en
  and and_15 (and_15_out, ENABLE, multiplexer_1_out);
  and and_16 (and_16_out, ENABLE, multiplexer_2_out);
  not not_11 (not_11_out, out_6[0]);
  Hex_Digit_Display hex_digit_display_3 (.value(out_6[15:12]));  // open: dp
  Hex_Digit_Display hex_digit_display_4 (.value(out_6[11:8]));  // open: dp
  Multiplexer #(.select(2)) multiplexer_3 (
    .in0(1'b0), .in1(not_11_out), .in2(not_11_out), .in3(in_1[0]), .out(multiplexer_3_out),
    .sel(Function_Selector));  // open: en
  Multiplexer #(.select(2)) multiplexer_4 (
    .in0(1'b0), .in1(xor_1_out), .in2(xor_2_out), .in3(in_1[1]), .out(multiplexer_4_out),
    .sel(Function_Selector));  // open: en
  Multiplexer #(.select(2)) multiplexer_5 (
    .in0(1'b0), .in1(xor_18_out), .in2(xor_19_out), .in3(in_1[2]), .out(multiplexer_5_out),
    .sel(Function_Selector));  // open: en
  Multiplexer #(.select(2)) multiplexer_6 (
    .in0(1'b0), .in1(xor_20_out), .in2(xor_21_out), .in3(in_1[3]), .out(multiplexer_6_out),
    .sel(Function_Selector));  // open: en
  Multiplexer #(.select(2)) multiplexer_7 (
    .in0(1'b0), .in1(xor_22_out), .in2(xor_23_out), .in3(in_1[4]), .out(multiplexer_7_out),
    .sel(Function_Selector));  // open: en
  Multiplexer #(.select(2)) multiplexer_8 (
    .in0(1'b0), .in1(xor_24_out), .in2(xor_25_out), .in3(in_1[5]), .out(multiplexer_8_out),
    .sel(Function_Selector));  // open: en
  Multiplexer #(.select(2)) multiplexer_9 (
    .in0(1'b0), .in1(xor_26_out), .in2(xor_27_out), .in3(in_1[6]), .out(multiplexer_9_out),
    .sel(Function_Selector));  // open: en
  Multiplexer #(.select(2)) multiplexer_10 (
    .in0(1'b0), .in1(xor_28_out), .in2(xor_29_out), .in3(in_1[7]), .out(multiplexer_10_out),
    .sel(Function_Selector));  // open: en
  Multiplexer #(.select(2)) multiplexer_11 (
    .in0(1'b0), .in1(xor_3_out), .in2(xor_4_out), .in3(in_1[0]), .out(multiplexer_11_out),
    .sel(Function_Selector));  // open: en
  Multiplexer #(.select(2)) multiplexer_12 (
    .in0(1'b0), .in1(xor_5_out), .in2(xor_6_out), .in3(in_1[1]), .out(multiplexer_12_out),
    .sel(Function_Selector));  // open: en
  Multiplexer #(.select(2)) multiplexer_13 (
    .in0(1'b0), .in1(xor_7_out), .in2(xor_8_out), .in3(in_1[2]), .out(multiplexer_13_out),
    .sel(Function_Selector));  // open: en
  Multiplexer #(.select(2)) multiplexer_14 (
    .in0(1'b0), .in1(xor_9_out), .in2(xor_10_out), .in3(in_1[3]), .out(multiplexer_14_out),
    .sel(Function_Selector));  // open: en
  Multiplexer #(.select(2)) multiplexer_15 (
    .in0(1'b0), .in1(xor_11_out), .in2(xor_12_out), .in3(in_1[4]), .out(multiplexer_15_out),
    .sel(Function_Selector));  // open: en
  Multiplexer #(.select(2)) multiplexer_16 (
    .in0(1'b0), .in1(xor_13_out), .in2(xor_14_out), .in3(in_1[5]), .out(multiplexer_16_out),
    .sel(Function_Selector));  // open: en
  Multiplexer #(.select(2)) multiplexer_17 (
    .in0(1'b0), .in1(xor_15_out), .in2(xor_16_out), .in3(in_1[6]), .out(multiplexer_17_out),
    .sel(Function_Selector));  // open: en
  Multiplexer #(.select(2)) multiplexer_18 (
    .in0(1'b0), .in1(xor_17_out), .in2(xor_30_out), .in3(in_1[7]), .out(multiplexer_18_out),
    .sel(Function_Selector));  // open: en
  Hex_Digit_Display hex_digit_display_5 (.value(out_6[7:4]));  // open: dp
  Hex_Digit_Display hex_digit_display_6 (.value(out_6[3:0]));  // open: dp
  D_Flip_Flop d_ff_1 (.clk(CLK), .D(multiplexer_3_out), .Q(out_6[0]), .en(and_15_out));  // open: Qn, preset, reset
  D_Flip_Flop d_ff_2 (.clk(CLK), .D(multiplexer_4_out), .Q(out_6[1]), .en(and_15_out));  // open: Qn, preset, reset
  D_Flip_Flop d_ff_3 (.clk(CLK), .D(multiplexer_5_out), .Q(out_6[2]), .en(and_15_out));  // open: Qn, preset, reset
  D_Flip_Flop d_ff_4 (.clk(CLK), .D(multiplexer_6_out), .Q(out_6[3]), .en(and_15_out));  // open: Qn, preset, reset
  D_Flip_Flop d_ff_5 (.clk(CLK), .D(multiplexer_7_out), .Q(out_6[4]), .en(and_15_out));  // open: Qn, preset, reset
  D_Flip_Flop d_ff_6 (.clk(CLK), .D(multiplexer_8_out), .Q(out_6[5]), .en(and_15_out));  // open: Qn, preset, reset
  D_Flip_Flop d_ff_7 (.clk(CLK), .D(multiplexer_9_out), .Q(out_6[6]), .en(and_15_out));  // open: Qn, preset, reset
  D_Flip_Flop d_ff_8 (.clk(CLK), .D(multiplexer_10_out), .Q(out_6[7]), .en(and_15_out));  // open: Qn, preset, reset
  D_Flip_Flop d_ff_9 (.clk(CLK), .D(multiplexer_11_out), .Q(out_6[8]), .en(and_16_out));  // open: Qn, preset, reset
  D_Flip_Flop d_ff_10 (.clk(CLK), .D(multiplexer_12_out), .Q(out_6[9]), .en(and_16_out));  // open: Qn, preset, reset
  D_Flip_Flop d_ff_11 (.clk(CLK), .D(multiplexer_13_out), .Q(out_6[10]), .en(and_16_out));  // open: Qn, preset, reset
  D_Flip_Flop d_ff_12 (.clk(CLK), .D(multiplexer_14_out), .Q(out_6[11]), .en(and_16_out));  // open: Qn, preset, reset
  D_Flip_Flop d_ff_13 (.clk(CLK), .D(multiplexer_15_out), .Q(out_6[12]), .en(and_16_out));  // open: Qn, preset, reset
  D_Flip_Flop d_ff_14 (.clk(CLK), .D(multiplexer_16_out), .Q(out_6[13]), .en(and_16_out));  // open: Qn, preset, reset
  D_Flip_Flop d_ff_15 (.clk(CLK), .D(multiplexer_17_out), .Q(out_6[14]), .en(and_16_out));  // open: Qn, preset, reset
  D_Flip_Flop d_ff_16 (.clk(CLK), .D(multiplexer_18_out), .Q(out_6[15]), .en(and_16_out));  // open: Qn, preset, reset

  // Notes on the sheet:
  //   INPUT
  //   REGISTER
  //   Low IR enables
  //   Hıgh IR enables
endmodule
