// Logisim project part2_edited.circ as structural Verilog: 1 circuit, main circuit main
module main (
  input  MuxCSel,
  input  in_2,
  input  [3:0] FunSel,
  input  [1:0] OutASel,
  input  [1:0] OutBSel,
  input  [1:0] FunSel_2,
  input  [3:0] RegSel,
  input  [1:0] MuxASel,
  input  [1:0] MuxBSel,
  input  in_10,
  input  in_11,
  input  in_12,
  input  in_13,
  input  [1:0] OutCSel,
  input  [1:0] OutDSel,
  input  [1:0] FunSel_3,
  input  [3:0] RegSel_2,
  input  L_H,
  input  Enable,
  input  [1:0] FunSel_4,
  output [7:0] out_21,
  output [3:0] out_22,
  output [15:0] out_23
);

  wire [3:0] main_2_out_6;
  wire [7:0] multiplexer_1_out, multiplexer_2_out, multiplexer_3_out, n3_register_bank_1_out_7,
       n3_register_bank_1_out_8, n4_register_bank_1_out_7, n4_register_bank_1_out_8, ram_1_data;

  Multiplexer #(.select(2), .width(8), .enable("false")) multiplexer_1 (
    .in0(out_23[7:0]), .in1(ram_1_data), .in2(n3_register_bank_1_out_7), .in3(out_21),
    .out(multiplexer_1_out), .sel(MuxASel));
  _4_register_bank u_4_register_bank_1 (
    .RegSel(RegSel), .CLK(in_2), .in_3(multiplexer_1_out), .Funsel(FunSel_2), .OutCSel(OutASel),
    .OutDSel(OutBSel), .out_7(n4_register_bank_1_out_7), .out_8(n4_register_bank_1_out_8));
  Multiplexer #(.select(2), .width(8), .enable("false")) multiplexer_2 (
    .in0(out_23[7:0]), .in1(out_23[7:0]), .in2(ram_1_data), .in3(out_21), .out(multiplexer_2_out),
    .sel(MuxBSel));
  _2c_main main_1 (
    .in_1(ram_1_data), .out_6(out_23), .ENABLE(Enable), .CLK(in_2), .Function_Selector(FunSel_4), .L_H(L_H));
  Multiplexer #(.width(8), .enable("false")) multiplexer_3 (
    .in0(multiplexer_1_out), .in1(n4_register_bank_1_out_7), .out(multiplexer_3_out), .sel(MuxCSel));
  alu2_main main_2 (
    .Out(out_21), .FunSel(FunSel), .A(multiplexer_3_out), .B(n4_register_bank_1_out_8), .in_4(out_22[2]),
    .out_6(main_2_out_6));
  _3_register_bank u_3_register_bank_1 (
    .RegSel(RegSel_2), .CLK(in_2), .in_3(multiplexer_2_out), .Funsel(FunSel_3), .OutCSel(OutCSel),
    .OutDSel(OutDSel), .out_7(n3_register_bank_1_out_7), .out_8(n3_register_bank_1_out_8));
  Register #(.width(1)) register_1 (.D(main_2_out_6[3]), .en(1'b1), .Q(out_22[3]), .clk(in_2));  // open: clr
  RAM #(.bus("separate")) ram_1 (
    .addr(n3_register_bank_1_out_8), .din(out_21), .data(ram_1_data), .str(in_10), .sel(in_11), .clk(in_2),
    .ld(in_12), .clr(in_13));
  Register #(.width(1)) register_2 (.D(main_2_out_6[2]), .en(1'b1), .Q(out_22[2]), .clk(in_2));  // open: clr
  Register #(.width(1)) register_3 (.D(main_2_out_6[1]), .en(1'b1), .Q(out_22[1]), .clk(in_2));  // open: clr
  Register #(.width(1)) register_4 (.D(main_2_out_6[0]), .en(1'b1), .Q(out_22[0]), .clk(in_2));  // open: clr

  // Notes on the sheet:
  //   A
  //   B
  //   C
endmodule
