// Logisim project project3.circ as structural Verilog: 3 circuits, main circuit main
// T0
module main (
  output [15:0] out_1
);

  wire and_1_out, and_2_out, and_3_out, and_4_out, and_5_out, and_6_out, and_7_out, and_8_out, and_9_out,
       and_10_out, and_11_out, and_12_out, and_13_out, and_14_out, and_15_out, and_16_out, and_17_out,
       and_18_out, and_19_out, and_20_out, and_21_out, and_22_out, and_23_out, and_24_out, and_25_out,
       and_26_out, and_27_out, and_28_out, and_29_out, and_30_out, and_31_out, and_32_out, and_33_out,
       and_34_out, and_35_out, and_36_out, and_37_out, and_38_out, and_39_out, and_40_out, and_41_out,
       and_42_out, and_43_out, and_44_out, and_45_out, and_46_out, and_47_out, and_48_out, and_49_out,
       and_50_out, and_51_out, and_52_out, and_53_out, and_54_out, and_55_out, and_56_out, and_57_out,
       and_58_out, and_59_out, and_60_out, and_61_out, and_62_out, and_63_out, and_64_out, and_65_out,
       and_66_out, and_67_out, and_68_out, and_69_out, and_70_out, and_71_out, and_72_out, and_73_out,
       and_74_out, and_75_out, and_76_out, and_77_out, and_78_out, and_79_out, and_80_out, and_81_out,
       and_82_out, and_83_out, and_84_out, and_85_out, and_86_out, and_87_out, and_88_out, and_89_out,
       and_90_out, and_91_out, and_92_out, and_93_out, and_94_out, and_95_out, and_96_out, and_97_out,
       and_98_out, and_99_out, and_100_out, and_101_out, and_102_out, and_103_out, and_104_out, and_105_out,
       and_106_out, and_107_out, and_108_out, and_109_out, and_110_out, and_111_out, and_112_out,
       and_113_out, and_114_out, and_115_out, and_116_out, and_117_out, and_118_out, and_119_out,
       and_120_out, and_121_out, and_122_out, and_123_out, and_124_out, and_125_out, clock_1_out, D0_LD,
       D1_ST, D2_MOV, D3_PSH, D4_PUL, D5_ADD, D6_SUB, D7_DEC, D8_INC, D9_AND, D10_OR, D11_NOT, D12_LSL,
       D13_LSR, D14_BRA, D15_BEQ, D16_BNE, D17_CALL, D18_RET, decoder_4_out0, decoder_4_out1, decoder_5_out0,
       decoder_5_out1, decoder_6_out0, decoder_6_out1, decoder_8_out0, decoder_8_out1, decoder_9_out0,
       decoder_9_out1, decoder_11_out0, decoder_11_out1, decoder_12_out0, decoder_12_out1, decoder_13_out0,
       decoder_13_out1, decoder_19_out0, decoder_19_out1, decoder_24_out0, decoder_24_out1, decoder_25_out0,
       decoder_25_out1, decoder_27_out0, decoder_27_out1, decoder_28_out0, decoder_28_out1, decoder_32_out0,
       decoder_32_out1, decoder_33_out0, decoder_33_out1, decoder_34_out0, decoder_34_out1, decoder_35_out0,
       decoder_35_out1, decoder_36_out0, decoder_36_out1, decoder_37_out0, decoder_37_out1, decoder_38_out0,
       decoder_38_out1, decoder_39_out0, decoder_39_out1, decoder_51_out0, decoder_51_out1, decoder_52_out0,
       decoder_52_out1, decoder_53_out0, decoder_53_out1, decoder_54_out0, decoder_54_out1, decoder_55_out0,
       decoder_55_out1, decoder_56_out0, decoder_56_out1, decoder_60_out0, decoder_60_out1, decoder_61_out0,
       decoder_61_out1, IR_EN, IR_LH, MEM_CLR, MEM_LD, MEM_SEL, MEM_STR, MuxCSel, not_1_out, not_2_out,
       not_3_out, not_4_out, not_5_out, not_6_out, not_7_out, not_8_out, not_9_out, not_10_out, not_11_out,
       not_12_out, not_13_out, not_14_out, not_15_out, not_16_out, not_17_out, not_18_out, not_19_out,
       not_20_out, not_21_out, not_22_out, not_23_out, not_24_out, not_25_out, not_26_out, not_27_out,
       not_28_out, not_29_out, not_30_out, not_31_out, not_32_out, not_33_out, not_34_out, not_35_out,
       not_36_out, not_37_out, not_38_out, not_39_out, not_40_out, not_41_out, not_42_out, not_43_out,
       not_44_out, not_45_out, not_46_out, not_47_out, not_48_out, not_49_out, not_50_out, not_51_out,
       not_52_out, not_53_out, not_54_out, not_55_out, not_56_out, not_57_out, not_58_out, not_59_out,
       not_60_out, not_61_out, not_62_out, not_63_out, not_64_out, not_65_out, not_66_out, not_67_out,
       not_68_out, not_69_out, not_70_out, not_71_out, not_72_out, not_73_out, not_74_out, not_75_out,
       not_76_out, not_77_out, not_78_out, not_79_out, or_4_out, or_7_out, or_24_out, or_25_out, or_30_out,
       or_35_out, SCR, T0, T1, T2, T3, T4, T5, T6, T7;
  wire [1:0] _3RB_FS, _4RB_FS, controlled_buffer_7_out, controlled_buffer_14_out, controlled_buffer_37_out,
       controlled_buffer_42_out, controlled_buffer_44_out, controlled_buffer_48_out,
       controlled_buffer_56_out, controlled_buffer_71_out, controlled_buffer_79_out,
       controlled_buffer_93_out, controlled_buffer_96_out, controlled_buffer_97_out,
       controlled_buffer_105_out, controlled_buffer_128_out, controlled_buffer_135_out,
       controlled_buffer_203_out, controlled_buffer_211_out, controlled_buffer_224_out,
       controlled_buffer_230_out, controlled_buffer_241_out, controlled_buffer_260_out,
       controlled_buffer_266_out, controlled_buffer_272_out, controlled_buffer_280_out,
       controlled_buffer_298_out, controlled_buffer_306_out, controlled_buffer_322_out,
       controlled_buffer_329_out, controlled_buffer_336_out, controlled_buffer_342_out,
       controlled_buffer_347_out, controlled_buffer_349_out, controlled_buffer_355_out,
       controlled_buffer_360_out, controlled_buffer_363_out, controlled_buffer_365_out,
       controlled_buffer_373_out, controlled_buffer_422_out, controlled_buffer_430_out,
       controlled_buffer_436_out, controlled_buffer_450_out, controlled_buffer_466_out,
       controlled_buffer_472_out, controlled_buffer_486_out, controlled_buffer_492_out,
       controlled_buffer_497_out, controlled_buffer_499_out, controlled_buffer_505_out,
       controlled_buffer_510_out, controlled_buffer_515_out, controlled_buffer_517_out,
       controlled_buffer_527_out, controlled_buffer_531_out, controlled_buffer_549_out,
       controlled_buffer_555_out, controlled_buffer_560_out, IR_FS, MuxASel, MuxBSel, OutASel, OutBSel,
       outcdecoder_2_out_2, outcdecoder_3_out_2, outcdecoder_4_out_2, outcdecoder_5_out_2,
       outcdecoder_7_out_2, outcdecoder_8_out_2, outcdecoder_9_out_2, outcdecoder_10_out_2,
       outcdecoder_11_out_2, outcdecoder_14_out_2, outcdecoder_15_out_2, outcdecoder_16_out_2,
       outcdecoder_17_out_2, outcdecoder_21_out_2, outcdecoder_22_out_2, outcdecoder_23_out_2,
       outcdecoder_24_out_2, OutCSel, OutDSel;
  wire [2:0] controlled_buffer_244_out, controlled_buffer_258_out, controlled_buffer_264_out,
       controlled_buffer_270_out, controlled_buffer_289_out, controlled_buffer_291_out,
       controlled_buffer_296_out, controlled_buffer_318_out, controlled_buffer_434_out,
       controlled_buffer_448_out, controlled_buffer_454_out, controlled_buffer_460_out,
       controlled_buffer_478_out, controlled_buffer_482_out, controlled_buffer_484_out,
       controlled_buffer_535_out, controlled_buffer_541_out, controlled_buffer_547_out;
  wire [3:0] _3RB_RS, _4RB_RS, ALUFlags, ALUFS;

  counter counter_1 (
    .out_2(T0), .out_3(T1), .out_4(T2), .out_5(T3), .out_6(T4), .out_7(T5), .out_8(T6), .out_9(T7), .in_1(SCR));
  and and_1 (and_1_out, D14_BRA, T3);
  assign MuxBSel = and_1_out ? 2'b01 : 2'bz;  // Controlled_Buffer controlled_buffer_1
  assign _3RB_FS = and_1_out ? 2'b01 : 2'bz;  // Controlled_Buffer controlled_buffer_2
  assign _3RB_RS = and_1_out ? 4'b0001 : 4'bz;  // Controlled_Buffer controlled_buffer_3
  assign MEM_SEL = and_1_out ? 1'b0 : 1'bz;  // Controlled_Buffer controlled_buffer_4
  assign MEM_LD = and_1_out ? 1'b0 : 1'bz;  // Controlled_Buffer controlled_buffer_5
  assign MEM_STR = and_1_out ? 1'b0 : 1'bz;  // Controlled_Buffer controlled_buffer_6
  not not_1 (not_1_out, out_1[8]);
  and and_2 (and_2_out, D0_LD, not_1_out, T3);
  assign controlled_buffer_7_out = and_2_out ? out_1[10:9] : 2'bz;  // Controlled_Buffer controlled_buffer_7
  assign MuxASel = and_2_out ? 2'b00 : 2'bz;  // Controlled_Buffer controlled_buffer_8
  assign _4RB_FS = and_2_out ? 2'b01 : 2'bz;  // Controlled_Buffer controlled_buffer_9
  not not_2 (not_2_out, out_1[10]);
  and and_3 (and_3_out, D2_MOV, T3, not_2_out, not_3_out);
  assign OutASel = and_3_out ? out_1[6:5] : 2'bz;  // Controlled_Buffer controlled_buffer_10
  assign MuxCSel = and_3_out ? 1'b1 : 1'bz;  // Controlled_Buffer controlled_buffer_11
  assign ALUFS = and_3_out ? 4'b0000 : 4'bz;  // Controlled_Buffer controlled_buffer_12
  assign MuxASel = and_3_out ? 2'b11 : 2'bz;  // Controlled_Buffer controlled_buffer_13
  Decoder #(.select(2)) decoder_1 (
    .out0(_4RB_RS[0]), .out1(_4RB_RS[1]), .out2(_4RB_RS[2]), .out3(_4RB_RS[3]),
    .sel(controlled_buffer_14_out), .en(and_3_out));
  assign controlled_buffer_14_out = and_3_out ? out_1[9:8] : 2'bz;  // Controlled_Buffer controlled_buffer_14
  assign _4RB_FS = and_3_out ? 2'b01 : 2'bz;  // Controlled_Buffer controlled_buffer_15
  assign MEM_SEL = T0 ? 1'b1 : 1'bz;  // Controlled_Buffer controlled_buffer_16
  assign MEM_LD = T0 ? 1'b1 : 1'bz;  // Controlled_Buffer controlled_buffer_17
  assign _3RB_FS = T0 ? 2'b10 : 2'bz;  // Controlled_Buffer controlled_buffer_18
  assign _3RB_RS = T0 ? 4'b0001 : 4'bz;  // Controlled_Buffer controlled_buffer_19
  assign IR_EN = T0 ? 1'b1 : 1'bz;  // Controlled_Buffer controlled_buffer_20
  assign IR_FS = T0 ? 2'b11 : 2'bz;  // Controlled_Buffer controlled_buffer_21
  assign IR_LH = T0 ? 1'b0 : 1'bz;  // Controlled_Buffer controlled_buffer_22
  assign MEM_STR = T0 ? 1'b0 : 1'bz;  // Controlled_Buffer controlled_buffer_23
  assign OutDSel = T0 ? 2'b00 : 2'bz;  // Controlled_Buffer controlled_buffer_24
  assign MEM_CLR = T0 ? 1'b0 : 1'bz;  // Controlled_Buffer controlled_buffer_25
  Decoder #(.select(5), .enable("false")) decoder_2 (
    .out0(D0_LD), .out1(D1_ST), .out2(D2_MOV), .out3(D3_PSH), .out4(D4_PUL), .out5(D5_ADD), .out6(D6_SUB),
    .out7(D7_DEC), .out8(D8_INC), .out9(D9_AND), .out10(D10_OR), .out11(D11_NOT), .out12(D12_LSL),
    .out13(D13_LSR), .out14(D14_BRA), .out15(D15_BEQ), .out16(D16_BNE), .out17(D17_CALL), .out18(D18_RET),
    .sel(out_1[15:11]));  // open: out19, out20, out21, out22, out23, out24, out25, out26, out27, out28, out29, out30, out31
  Decoder #(.select(2)) decoder_3 (
    .out0(_4RB_RS[0]), .out1(_4RB_RS[1]), .out2(_4RB_RS[2]), .out3(_4RB_RS[3]),
    .sel(controlled_buffer_7_out), .en(and_2_out));
  not not_3 (not_3_out, out_1[7]);
  and and_4 (and_4_out, D14_BRA, T4);
  assign SCR = and_4_out ? 1'b1 : 1'bz;  // Controlled_Buffer controlled_buffer_26
  and and_5 (and_5_out, D5_ADD, T3, out_1[10]);
  and and_6 (and_6_out, D6_SUB, T3, out_1[10]);
  and and_7 (and_7_out, and_6_out, out_1[4]);
  and and_8 (and_8_out, and_5_out, out_1[7]);
  and and_9 (and_9_out, and_5_out, out_1[4]);
  and and_10 (and_10_out, and_6_out, out_1[7]);
  not not_4 (not_4_out, out_1[4]);
  assign IR_LH = T1 ? 1'b1 : 1'bz;  // Controlled_Buffer controlled_buffer_27
  assign _3RB_RS = T1 ? 4'b0001 : 4'bz;  // Controlled_Buffer controlled_buffer_28
  assign OutDSel = T1 ? 2'b00 : 2'bz;  // Controlled_Buffer controlled_buffer_29
  assign MEM_SEL = T1 ? 1'b1 : 1'bz;  // Controlled_Buffer controlled_buffer_30
  assign MEM_LD = T1 ? 1'b1 : 1'bz;  // Controlled_Buffer controlled_buffer_31
  assign IR_EN = T1 ? 1'b1 : 1'bz;  // Controlled_Buffer controlled_buffer_32
  assign IR_FS = T1 ? 2'b11 : 2'bz;  // Controlled_Buffer controlled_buffer_33
  assign _3RB_FS = T1 ? 2'b10 : 2'bz;  // Controlled_Buffer controlled_buffer_34
  assign MEM_STR = T1 ? 1'b0 : 1'bz;  // Controlled_Buffer controlled_buffer_35
  assign MEM_CLR = T1 ? 1'b0 : 1'bz;  // Controlled_Buffer controlled_buffer_36
  and and_11 (and_11_out, D2_MOV, T3, out_1[10], out_1[7]);
  assign controlled_buffer_37_out = and_11_out ? out_1[6:5] : 2'bz;  // Controlled_Buffer controlled_buffer_37
  assign MuxASel = and_11_out ? 2'b10 : 2'bz;  // Controlled_Buffer controlled_buffer_38
  assign MuxCSel = and_11_out ? 1'b0 : 1'bz;  // Controlled_Buffer controlled_buffer_39
  assign ALUFS = and_11_out ? 4'b0000 : 4'bz;  // Controlled_Buffer controlled_buffer_40
  assign MuxBSel = and_11_out ? 2'b11 : 2'bz;  // Controlled_Buffer controlled_buffer_41
  assign controlled_buffer_42_out = and_11_out ? out_1[9:8] : 2'bz;  // Controlled_Buffer controlled_buffer_42
  assign _3RB_FS = and_11_out ? 2'b01 : 2'bz;  // Controlled_Buffer controlled_buffer_43
  not not_5 (not_5_out, out_1[7]);
  not not_6 (not_6_out, out_1[4]);
  and and_12 (and_12_out, and_6_out, not_7_out, not_4_out);
  not not_7 (not_7_out, out_1[7]);
  and and_13 (and_13_out, D0_LD, out_1[8], T3);
  assign controlled_buffer_44_out = and_13_out ? out_1[10:9] : 2'bz;  // Controlled_Buffer controlled_buffer_44
  assign MuxASel = and_13_out ? 2'b01 : 2'bz;  // Controlled_Buffer controlled_buffer_45
  assign _4RB_FS = and_13_out ? 2'b01 : 2'bz;  // Controlled_Buffer controlled_buffer_46
  assign OutDSel = and_13_out ? 2'b01 : 2'bz;  // Controlled_Buffer controlled_buffer_47
  outcdecoder outcdecoder_1 (.in_1(controlled_buffer_37_out), .out_2(OutCSel));
  Decoder #(.select(2), .disabled(0)) decoder_4 (
    .out0(decoder_4_out0), .out1(decoder_4_out1), .out2(_3RB_RS[1]), .out3(_3RB_RS[2]),
    .sel(controlled_buffer_42_out), .en(and_11_out));
  or or_1 (_3RB_RS[0], decoder_4_out0, decoder_4_out1);
  and and_14 (and_14_out, D15_BEQ, ALUFlags[3]);
  outcdecoder outcdecoder_2 (.in_1(out_1[6:5]), .out_2(outcdecoder_2_out_2));
  and and_15 (and_15_out, and_5_out, not_5_out, not_6_out);
  outcdecoder outcdecoder_3 (.in_1(out_1[3:2]), .out_2(outcdecoder_3_out_2));
  Decoder #(.select(2), .disabled(0)) decoder_5 (
    .out0(decoder_5_out0), .out1(decoder_5_out1), .out2(_3RB_RS[1]), .out3(_3RB_RS[2]),
    .sel(controlled_buffer_48_out), .en(and_10_out));
  assign controlled_buffer_48_out = and_10_out ? out_1[9:8] : 2'bz;  // Controlled_Buffer controlled_buffer_48
  or or_2 (_3RB_RS[0], decoder_5_out0, decoder_5_out1);
  assign _3RB_FS = and_10_out ? 2'b01 : 2'bz;  // Controlled_Buffer controlled_buffer_49
  assign MuxBSel = and_10_out ? 2'b11 : 2'bz;  // Controlled_Buffer controlled_buffer_50
  assign ALUFS = and_10_out ? 4'b0110 : 4'bz;  // Controlled_Buffer controlled_buffer_51
  assign MuxASel = and_10_out ? 2'b10 : 2'bz;  // Controlled_Buffer controlled_buffer_52
  assign OutBSel = and_10_out ? out_1[3:2] : 2'bz;  // Controlled_Buffer controlled_buffer_53
  assign OutCSel = and_10_out ? outcdecoder_4_out_2 : 2'bz;  // Controlled_Buffer controlled_buffer_54
  outcdecoder outcdecoder_4 (.in_1(out_1[6:5]), .out_2(outcdecoder_4_out_2));
  assign MuxCSel = and_10_out ? 1'b0 : 1'bz;  // Controlled_Buffer controlled_buffer_55
  Decoder #(.select(2), .disabled(0)) decoder_6 (
    .out0(decoder_6_out0), .out1(decoder_6_out1), .out2(_3RB_RS[1]), .out3(_3RB_RS[2]),
    .sel(controlled_buffer_56_out), .en(and_7_out));
  assign controlled_buffer_56_out = and_7_out ? out_1[9:8] : 2'bz;  // Controlled_Buffer controlled_buffer_56
  or or_3 (_3RB_RS[0], decoder_6_out0, decoder_6_out1);
  assign _3RB_FS = and_7_out ? 2'b01 : 2'bz;  // Controlled_Buffer controlled_buffer_57
  assign MuxBSel = and_7_out ? 2'b11 : 2'bz;  // Controlled_Buffer controlled_buffer_58
  assign ALUFS = and_7_out ? 4'b0110 : 4'bz;  // Controlled_Buffer controlled_buffer_59
  assign MuxASel = and_7_out ? 2'b10 : 2'bz;  // Controlled_Buffer controlled_buffer_60
  assign OutBSel = and_7_out ? out_1[6:5] : 2'bz;  // Controlled_Buffer controlled_buffer_61
  outcdecoder outcdecoder_5 (.in_1(out_1[3:2]), .out_2(outcdecoder_5_out_2));
  assign OutCSel = and_7_out ? outcdecoder_5_out_2 : 2'bz;  // Controlled_Buffer controlled_buffer_62
  assign MuxCSel = and_7_out ? 1'b0 : 1'bz;  // Controlled_Buffer controlled_buffer_63
  assign IR_EN = T2 ? 1'b0 : 1'bz;  // Controlled_Buffer controlled_buffer_64
  Decoder #(.select(2)) decoder_7 (
    .out0(_4RB_RS[0]), .out1(_4RB_RS[1]), .out2(_4RB_RS[2]), .out3(_4RB_RS[3]),
    .sel(controlled_buffer_44_out), .en(and_13_out));
  not not_8 (not_8_out, ALUFlags[3]);
  and and_16 (and_16_out, not_8_out, D16_BNE);
  or or_4 (or_4_out, and_14_out, and_16_out);
  and and_17 (and_17_out, or_4_out, T3);
  assign MuxBSel = and_17_out ? 2'b01 : 2'bz;  // Controlled_Buffer controlled_buffer_65
  assign _3RB_FS = and_17_out ? 2'b01 : 2'bz;  // Controlled_Buffer controlled_buffer_66
  assign _3RB_RS = and_17_out ? 4'b0001 : 4'bz;  // Controlled_Buffer controlled_buffer_67
  assign MEM_SEL = and_17_out ? 1'b0 : 1'bz;  // Controlled_Buffer controlled_buffer_68
  assign MEM_LD = and_17_out ? 1'b0 : 1'bz;  // Controlled_Buffer controlled_buffer_69
  assign MEM_STR = and_17_out ? 1'b0 : 1'bz;  // Controlled_Buffer controlled_buffer_70
  Decoder #(.select(2), .disabled(0)) decoder_8 (
    .out0(decoder_8_out0), .out1(decoder_8_out1), .out2(_3RB_RS[1]), .out3(_3RB_RS[2]),
    .sel(controlled_buffer_71_out), .en(and_8_out));
  assign controlled_buffer_71_out = and_8_out ? out_1[9:8] : 2'bz;  // Controlled_Buffer controlled_buffer_71
  or or_5 (_3RB_RS[0], decoder_8_out0, decoder_8_out1);
  assign _3RB_FS = and_8_out ? 2'b01 : 2'bz;  // Controlled_Buffer controlled_buffer_72
  assign MuxBSel = and_8_out ? 2'b11 : 2'bz;  // Controlled_Buffer controlled_buffer_73
  assign ALUFS = and_8_out ? 4'b0100 : 4'bz;  // Controlled_Buffer controlled_buffer_74
  assign MuxASel = and_8_out ? 2'b10 : 2'bz;  // Controlled_Buffer controlled_buffer_75
  assign OutBSel = and_8_out ? out_1[3:2] : 2'bz;  // Controlled_Buffer controlled_buffer_76
  assign OutCSel = and_8_out ? outcdecoder_2_out_2 : 2'bz;  // Controlled_Buffer controlled_buffer_77
  assign MuxCSel = and_8_out ? 1'b0 : 1'bz;  // Controlled_Buffer controlled_buffer_78
  assign controlled_buffer_79_out = and_9_out ? out_1[9:8] : 2'bz;  // Controlled_Buffer controlled_buffer_79
  Decoder #(.select(2), .disabled(0)) decoder_9 (
    .out0(decoder_9_out0), .out1(decoder_9_out1), .out2(_3RB_RS[1]), .out3(_3RB_RS[2]),
    .sel(controlled_buffer_79_out), .en(and_9_out));
  or or_6 (_3RB_RS[0], decoder_9_out0, decoder_9_out1);
  assign _3RB_FS = and_9_out ? 2'b01 : 2'bz;  // Controlled_Buffer controlled_buffer_80
  assign MuxBSel = and_9_out ? 2'b11 : 2'bz;  // Controlled_Buffer controlled_buffer_81
  assign ALUFS = and_9_out ? 4'b0100 : 4'bz;  // Controlled_Buffer controlled_buffer_82
  assign MuxASel = and_9_out ? 2'b10 : 2'bz;  // Controlled_Buffer controlled_buffer_83
  assign OutBSel = and_9_out ? out_1[6:5] : 2'bz;  // Controlled_Buffer controlled_buffer_84
  assign OutCSel = and_9_out ? outcdecoder_3_out_2 : 2'bz;  // Controlled_Buffer controlled_buffer_85
  assign MuxCSel = and_9_out ? 1'b0 : 1'bz;  // Controlled_Buffer controlled_buffer_86
  or or_7 (or_7_out, D15_BEQ, D16_BNE);
  assign MEM_SEL = D0_LD ? 1'b1 : 1'bz;  // Controlled_Buffer controlled_buffer_87
  assign MEM_LD = D0_LD ? 1'b1 : 1'bz;  // Controlled_Buffer controlled_buffer_88
  assign MEM_STR = D0_LD ? 1'b0 : 1'bz;  // Controlled_Buffer controlled_buffer_89
  and and_18 (and_18_out, or_7_out, T4);
  assign SCR = and_18_out ? 1'b1 : 1'bz;  // Controlled_Buffer controlled_buffer_90
  and and_19 (and_19_out, D5_ADD, T4, out_1[10]);
  assign SCR = and_19_out ? 1'b1 : 1'bz;  // Controlled_Buffer controlled_buffer_91
  and and_20 (and_20_out, D6_SUB, T4, out_1[10]);
  assign SCR = and_20_out ? 1'b1 : 1'bz;  // Controlled_Buffer controlled_buffer_92
  Clock clock_1 (.out(clock_1_out));
  not not_9 (not_9_out, out_1[10]);
  and and_21 (and_21_out, D2_MOV, T3, not_9_out, out_1[7]);
  assign controlled_buffer_93_out = and_21_out ? out_1[6:5] : 2'bz;  // Controlled_Buffer controlled_buffer_93
  assign MuxASel = and_21_out ? 2'b10 : 2'bz;  // Controlled_Buffer controlled_buffer_94
  assign _4RB_FS = and_21_out ? 2'b01 : 2'bz;  // Controlled_Buffer controlled_buffer_95
  Decoder #(.select(2)) decoder_10 (
    .out0(_4RB_RS[0]), .out1(_4RB_RS[1]), .out2(_4RB_RS[2]), .out3(_4RB_RS[3]),
    .sel(controlled_buffer_96_out), .en(and_21_out));
  assign controlled_buffer_96_out = and_21_out ? out_1[9:8] : 2'bz;  // Controlled_Buffer controlled_buffer_96
  assign controlled_buffer_97_out = and_12_out ? out_1[9:8] : 2'bz;  // Controlled_Buffer controlled_buffer_97
  assign _3RB_FS = and_12_out ? 2'b01 : 2'bz;  // Controlled_Buffer controlled_buffer_98
  assign MuxBSel = and_12_out ? 2'b11 : 2'bz;  // Controlled_Buffer controlled_buffer_99
  assign ALUFS = and_12_out ? 4'b0110 : 4'bz;  // Controlled_Buffer controlled_buffer_100
  assign OutBSel = and_12_out ? out_1[3:2] : 2'bz;  // Controlled_Buffer controlled_buffer_101
  assign MuxCSel = and_12_out ? 1'b1 : 1'bz;  // Controlled_Buffer controlled_buffer_102
  assign OutASel = and_12_out ? out_1[6:5] : 2'bz;  // Controlled_Buffer controlled_buffer_103
  and and_22 (and_22_out, D0_LD, T4);
  assign SCR = and_22_out ? 1'b1 : 1'bz;  // Controlled_Buffer controlled_buffer_104
  outcdecoder outcdecoder_6 (.in_1(controlled_buffer_93_out), .out_2(OutCSel));
  assign controlled_buffer_105_out = and_15_out ? out_1[9:8] : 2'bz;  // Controlled_Buffer controlled_buffer_105
  Decoder #(.select(2), .disabled(0)) decoder_11 (
    .out0(decoder_11_out0), .out1(decoder_11_out1), .out2(_3RB_RS[1]), .out3(_3RB_RS[2]),
    .sel(controlled_buffer_105_out), .en(and_15_out));
  or or_8 (_3RB_RS[0], decoder_11_out0, decoder_11_out1);
  assign _3RB_FS = and_15_out ? 2'b01 : 2'bz;  // Controlled_Buffer controlled_buffer_106
  assign MuxBSel = and_15_out ? 2'b11 : 2'bz;  // Controlled_Buffer controlled_buffer_107
  assign ALUFS = and_15_out ? 4'b0100 : 4'bz;  // Controlled_Buffer controlled_buffer_108
  assign OutBSel = and_15_out ? out_1[3:2] : 2'bz;  // Controlled_Buffer controlled_buffer_109
  assign MuxCSel = and_15_out ? 1'b1 : 1'bz;  // Controlled_Buffer controlled_buffer_110
  assign OutASel = and_15_out ? out_1[6:5] : 2'bz;  // Controlled_Buffer controlled_buffer_111
  Decoder #(.select(2), .disabled(0)) decoder_12 (
    .out0(decoder_12_out0), .out1(decoder_12_out1), .out2(_3RB_RS[1]), .out3(_3RB_RS[2]),
    .sel(controlled_buffer_97_out), .en(and_12_out));
  or or_9 (_3RB_RS[0], decoder_12_out0, decoder_12_out1);
  and and_23 (and_23_out, D17_CALL, T3);
  assign MuxCSel = and_23_out ? 1'b0 : 1'bz;  // Controlled_Buffer controlled_buffer_112
  assign MuxASel = and_23_out ? 2'b10 : 2'bz;  // Controlled_Buffer controlled_buffer_113
  assign _3RB_FS = and_23_out ? 2'b01 : 2'bz;  // Controlled_Buffer controlled_buffer_114
  assign _3RB_RS = and_23_out ? 4'b0001 : 4'bz;  // Controlled_Buffer controlled_buffer_115
  assign MEM_SEL = and_23_out ? 1'b1 : 1'bz;  // Controlled_Buffer controlled_buffer_116
  assign MEM_LD = and_23_out ? 1'b1 : 1'bz;  // Controlled_Buffer controlled_buffer_117
  assign MEM_STR = and_23_out ? 1'b1 : 1'bz;  // Controlled_Buffer controlled_buffer_118
  assign OutDSel = and_23_out ? 2'b10 : 2'bz;  // Controlled_Buffer controlled_buffer_119
  assign OutCSel = and_23_out ? 2'b00 : 2'bz;  // Controlled_Buffer controlled_buffer_120
  assign MuxBSel = and_23_out ? 2'b01 : 2'bz;  // Controlled_Buffer controlled_buffer_121
  assign ALUFS = and_23_out ? 4'b0000 : 4'bz;  // Controlled_Buffer controlled_buffer_122
  part2_edited_main main_1 (
    .OutASel(OutASel), .OutBSel(OutBSel), .FunSel_2(_4RB_FS), .RegSel(_4RB_RS), .MuxASel(MuxASel),
    .OutCSel(OutCSel), .OutDSel(OutDSel), .FunSel_3(_3RB_FS), .RegSel_2(_3RB_RS), .L_H(IR_LH),
    .Enable(IR_EN), .FunSel_4(IR_FS), .MuxCSel(MuxCSel), .MuxBSel(MuxBSel), .FunSel(ALUFS), .in_10(MEM_STR),
    .in_11(MEM_SEL), .in_12(MEM_LD), .in_13(MEM_CLR), .out_22(ALUFlags), .out_23(out_1), .in_2(clock_1_out));  // open: out_21
  and and_24 (and_24_out, D2_MOV, T3, out_1[10], not_10_out);
  assign OutASel = and_24_out ? out_1[6:5] : 2'bz;  // Controlled_Buffer controlled_buffer_123
  assign MuxCSel = and_24_out ? 1'b1 : 1'bz;  // Controlled_Buffer controlled_buffer_124
  assign ALUFS = and_24_out ? 4'b0000 : 4'bz;  // Controlled_Buffer controlled_buffer_125
  assign MuxBSel = and_24_out ? 2'b11 : 2'bz;  // Controlled_Buffer controlled_buffer_126
  assign _3RB_FS = and_24_out ? 2'b01 : 2'bz;  // Controlled_Buffer controlled_buffer_127
  assign controlled_buffer_128_out = and_24_out ? out_1[9:8] : 2'bz;  // Controlled_Buffer controlled_buffer_128
  Decoder #(.select(2), .disabled(0)) decoder_13 (
    .out0(decoder_13_out0), .out1(decoder_13_out1), .out2(_3RB_RS[1]), .out3(_3RB_RS[2]),
    .sel(controlled_buffer_128_out), .en(and_24_out));
  or or_10 (_3RB_RS[0], decoder_13_out0, decoder_13_out1);
  not not_10 (not_10_out, out_1[7]);
  and and_25 (and_25_out, D17_CALL, T4);
  assign _3RB_FS = and_25_out ? 2'b11 : 2'bz;  // Controlled_Buffer controlled_buffer_129
  assign _3RB_RS = and_25_out ? 4'b0100 : 4'bz;  // Controlled_Buffer controlled_buffer_130
  assign MEM_STR = and_25_out ? 1'b0 : 1'bz;  // Controlled_Buffer controlled_buffer_131
  assign MuxBSel = and_25_out ? 2'b01 : 2'bz;  // Controlled_Buffer controlled_buffer_132
  Hex_Digit_Display hex_digit_display_1 (.value(out_1[15:12]));  // open: dp
  and and_26 (and_26_out, D17_CALL, T5);
  assign SCR = and_26_out ? 1'b1 : 1'bz;  // Controlled_Buffer controlled_buffer_133
  Hex_Digit_Display hex_digit_display_2 (.value(out_1[11:8]));  // open: dp
  Hex_Digit_Display hex_digit_display_3 (.value(out_1[7:4]));  // open: dp
  and and_27 (and_27_out, D2_MOV, T4);
  assign SCR = and_27_out ? 1'b1 : 1'bz;  // Controlled_Buffer controlled_buffer_134
  not not_11 (not_11_out, out_1[10]);
  and and_28 (and_28_out, D6_SUB, T3, not_11_out);
  Hex_Digit_Display hex_digit_display_4 (.value(out_1[3:0]));  // open: dp
  and and_29 (and_29_out, D1_ST, out_1[8], T3);
  assign controlled_buffer_135_out = and_29_out ? out_1[10:9] : 2'bz;  // Controlled_Buffer controlled_buffer_135
  Decoder #(.select(2)) decoder_14 (
    .out0(_4RB_RS[0]), .out1(_4RB_RS[1]), .out2(_4RB_RS[2]), .out3(_4RB_RS[3]),
    .sel(controlled_buffer_135_out), .en(and_29_out));
  assign OutBSel = and_29_out ? out_1[10:9] : 2'bz;  // Controlled_Buffer controlled_buffer_136
  assign ALUFS = and_29_out ? 4'b0001 : 4'bz;  // Controlled_Buffer controlled_buffer_137
  assign OutDSel = and_29_out ? 2'b01 : 2'bz;  // Controlled_Buffer controlled_buffer_138
  and and_30 (and_30_out, D18_RET, T3);
  assign _3RB_FS = and_30_out ? 2'b10 : 2'bz;  // Controlled_Buffer controlled_buffer_139
  assign _3RB_RS = and_30_out ? 4'b0100 : 4'bz;  // Controlled_Buffer controlled_buffer_140
  not not_12 (not_12_out, out_1[10]);
  and and_31 (and_31_out, D5_ADD, T3, not_12_out);
  and and_32 (and_32_out, and_31_out, out_1[4]);
  and and_33 (and_33_out, and_28_out, out_1[7]);
  and and_34 (and_34_out, and_28_out, out_1[4]);
  assign MEM_SEL = D2_MOV ? 1'b0 : 1'bz;  // Controlled_Buffer controlled_buffer_141
  assign MEM_LD = D2_MOV ? 1'b0 : 1'bz;  // Controlled_Buffer controlled_buffer_142
  assign MEM_STR = D2_MOV ? 1'b0 : 1'bz;  // Controlled_Buffer controlled_buffer_143
  and and_35 (and_35_out, and_31_out, out_1[7]);
  not not_13 (not_13_out, out_1[4]);
  not not_14 (not_14_out, out_1[7]);
  not not_15 (not_15_out, out_1[4]);
  assign MEM_SEL = D1_ST ? 1'b1 : 1'bz;  // Controlled_Buffer controlled_buffer_144
  assign MEM_LD = D1_ST ? 1'b1 : 1'bz;  // Controlled_Buffer controlled_buffer_145
  assign MEM_STR = D1_ST ? 1'b1 : 1'bz;  // Controlled_Buffer controlled_buffer_146
  and and_36 (and_36_out, D18_RET, T4);
  assign OutDSel = and_36_out ? 2'b10 : 2'bz;  // Controlled_Buffer controlled_buffer_147
  assign MuxBSel = and_36_out ? 2'b10 : 2'bz;  // Controlled_Buffer controlled_buffer_148
  assign _3RB_FS = and_36_out ? 2'b01 : 2'bz;  // Controlled_Buffer controlled_buffer_149
  assign _3RB_RS = and_36_out ? 4'b0001 : 4'bz;  // Controlled_Buffer controlled_buffer_150
  assign MEM_SEL = and_36_out ? 1'b1 : 1'bz;  // Controlled_Buffer controlled_buffer_151
  assign MEM_LD = and_36_out ? 1'b1 : 1'bz;  // Controlled_Buffer controlled_buffer_152
  and and_37 (and_37_out, and_31_out, not_16_out, not_13_out);
  not not_16 (not_16_out, out_1[7]);
  outcdecoder outcdecoder_7 (.in_1(out_1[6:5]), .out_2(outcdecoder_7_out_2));
  and and_38 (and_38_out, and_28_out, not_14_out, not_15_out);
  outcdecoder outcdecoder_8 (.in_1(out_1[3:2]), .out_2(outcdecoder_8_out_2));
  assign MEM_SEL = and_35_out ? 1'b1 : 1'bz;  // Controlled_Buffer controlled_buffer_153
  assign MEM_LD = and_35_out ? 1'b1 : 1'bz;  // Controlled_Buffer controlled_buffer_154
  assign MEM_STR = and_35_out ? 1'b1 : 1'bz;  // Controlled_Buffer controlled_buffer_155
  assign ALUFS = and_35_out ? 4'b0100 : 4'bz;  // Controlled_Buffer controlled_buffer_156
  assign MuxASel = and_35_out ? 2'b10 : 2'bz;  // Controlled_Buffer controlled_buffer_157
  assign OutBSel = and_35_out ? out_1[3:2] : 2'bz;  // Controlled_Buffer controlled_buffer_158
  assign OutCSel = and_35_out ? outcdecoder_9_out_2 : 2'bz;  // Controlled_Buffer controlled_buffer_159
  outcdecoder outcdecoder_9 (.in_1(out_1[6:5]), .out_2(outcdecoder_9_out_2));
  assign MuxCSel = and_35_out ? 1'b0 : 1'bz;  // Controlled_Buffer controlled_buffer_160
  assign OutDSel = and_35_out ? 2'b10 : 2'bz;  // Controlled_Buffer controlled_buffer_161
  assign MEM_SEL = and_32_out ? 1'b1 : 1'bz;  // Controlled_Buffer controlled_buffer_162
  assign MEM_LD = and_32_out ? 1'b1 : 1'bz;  // Controlled_Buffer controlled_buffer_163
  assign MEM_STR = and_32_out ? 1'b1 : 1'bz;  // Controlled_Buffer controlled_buffer_164
  assign ALUFS = and_32_out ? 4'b0100 : 4'bz;  // Controlled_Buffer controlled_buffer_165
  assign MuxASel = and_32_out ? 2'b10 : 2'bz;  // Controlled_Buffer controlled_buffer_166
  assign OutBSel = and_32_out ? out_1[6:5] : 2'bz;  // Controlled_Buffer controlled_buffer_167
  assign OutCSel = and_32_out ? outcdecoder_10_out_2 : 2'bz;  // Controlled_Buffer controlled_buffer_168
  outcdecoder outcdecoder_10 (.in_1(out_1[3:2]), .out_2(outcdecoder_10_out_2));
  assign MuxCSel = and_32_out ? 1'b0 : 1'bz;  // Controlled_Buffer controlled_buffer_169
  assign OutDSel = and_32_out ? 2'b10 : 2'bz;  // Controlled_Buffer controlled_buffer_170
  assign MEM_SEL = and_33_out ? 1'b1 : 1'bz;  // Controlled_Buffer controlled_buffer_171
  assign MEM_LD = and_33_out ? 1'b1 : 1'bz;  // Controlled_Buffer controlled_buffer_172
  assign MEM_STR = and_33_out ? 1'b1 : 1'bz;  // Controlled_Buffer controlled_buffer_173
  assign ALUFS = and_33_out ? 4'b0110 : 4'bz;  // Controlled_Buffer controlled_buffer_174
  assign MuxASel = and_33_out ? 2'b10 : 2'bz;  // Controlled_Buffer controlled_buffer_175
  assign OutBSel = and_33_out ? out_1[3:2] : 2'bz;  // Controlled_Buffer controlled_buffer_176
  assign OutCSel = and_33_out ? outcdecoder_7_out_2 : 2'bz;  // Controlled_Buffer controlled_buffer_177
  assign MuxCSel = and_33_out ? 1'b0 : 1'bz;  // Controlled_Buffer controlled_buffer_178
  assign OutDSel = and_33_out ? 2'b10 : 2'bz;  // Controlled_Buffer controlled_buffer_179
  assign MEM_SEL = and_34_out ? 1'b1 : 1'bz;  // Controlled_Buffer controlled_buffer_180
  assign MEM_LD = and_34_out ? 1'b1 : 1'bz;  // Controlled_Buffer controlled_buffer_181
  assign MEM_STR = and_34_out ? 1'b1 : 1'bz;  // Controlled_Buffer controlled_buffer_182
  assign ALUFS = and_34_out ? 4'b0110 : 4'bz;  // Controlled_Buffer controlled_buffer_183
  assign MuxASel = and_34_out ? 2'b10 : 2'bz;  // Controlled_Buffer controlled_buffer_184
  assign OutBSel = and_34_out ? out_1[6:5] : 2'bz;  // Controlled_Buffer controlled_buffer_185
  assign OutCSel = and_34_out ? outcdecoder_8_out_2 : 2'bz;  // Controlled_Buffer controlled_buffer_186
  assign MuxCSel = and_34_out ? 1'b0 : 1'bz;  // Controlled_Buffer controlled_buffer_187
  assign OutDSel = and_34_out ? 2'b10 : 2'bz;  // Controlled_Buffer controlled_buffer_188
  and and_39 (and_39_out, D3_PSH, T3);
  assign OutDSel = and_39_out ? 2'b10 : 2'bz;  // Controlled_Buffer controlled_buffer_189
  assign MEM_SEL = and_39_out ? 1'b1 : 1'bz;  // Controlled_Buffer controlled_buffer_190
  assign MEM_LD = and_39_out ? 1'b1 : 1'bz;  // Controlled_Buffer controlled_buffer_191
  assign MEM_STR = and_39_out ? 1'b1 : 1'bz;  // Controlled_Buffer controlled_buffer_192
  assign ALUFS = and_39_out ? 4'b0000 : 4'bz;  // Controlled_Buffer controlled_buffer_193
  and and_40 (and_40_out, and_39_out, out_1[10]);
  outcdecoder outcdecoder_11 (.in_1(out_1[9:8]), .out_2(outcdecoder_11_out_2));
  assign OutCSel = and_40_out ? outcdecoder_11_out_2 : 2'bz;  // Controlled_Buffer controlled_buffer_194
  assign MuxASel = and_40_out ? 2'b10 : 2'bz;  // Controlled_Buffer controlled_buffer_195
  assign MuxCSel = and_40_out ? 1'b0 : 1'bz;  // Controlled_Buffer controlled_buffer_196
  and and_41 (and_41_out, D18_RET, T5);
  assign SCR = and_41_out ? 1'b1 : 1'bz;  // Controlled_Buffer controlled_buffer_197
  and and_42 (and_42_out, not_14_out, not_15_out);
  and and_43 (and_43_out, D1_ST, T4);
  assign SCR = and_43_out ? 1'b1 : 1'bz;  // Controlled_Buffer controlled_buffer_198
  not not_17 (not_17_out, out_1[10]);
  and and_44 (and_44_out, and_39_out, not_17_out);
  and and_45 (and_45_out, not_16_out, not_13_out);
  and and_46 (and_46_out, D3_PSH, T4);
  assign _3RB_FS = and_46_out ? 2'b11 : 2'bz;  // Controlled_Buffer controlled_buffer_199
  assign _3RB_RS = and_46_out ? 4'b0100 : 4'bz;  // Controlled_Buffer controlled_buffer_200
  assign OutASel = and_44_out ? out_1[9:8] : 2'bz;  // Controlled_Buffer controlled_buffer_201
  assign MuxCSel = and_44_out ? 1'b1 : 1'bz;  // Controlled_Buffer controlled_buffer_202
  assign controlled_buffer_203_out = and_38_out ? out_1[9:8] : 2'bz;  // Controlled_Buffer controlled_buffer_203
  Decoder #(.select(2)) decoder_15 (
    .out0(_4RB_RS[0]), .out1(_4RB_RS[1]), .out2(_4RB_RS[2]), .out3(_4RB_RS[3]),
    .sel(controlled_buffer_203_out), .en(and_38_out));
  assign _4RB_FS = and_38_out ? 2'b01 : 2'bz;  // Controlled_Buffer controlled_buffer_204
  assign MuxASel = and_38_out ? 2'b11 : 2'bz;  // Controlled_Buffer controlled_buffer_205
  assign ALUFS = and_38_out ? 4'b0110 : 4'bz;  // Controlled_Buffer controlled_buffer_206
  assign OutBSel = and_38_out ? out_1[3:2] : 2'bz;  // Controlled_Buffer controlled_buffer_207
  assign _3RB_RS = and_38_out ? 4'b0000 : 4'bz;  // Controlled_Buffer controlled_buffer_208
  assign MuxCSel = and_38_out ? 1'b1 : 1'bz;  // Controlled_Buffer controlled_buffer_209
  assign OutASel = and_38_out ? out_1[6:5] : 2'bz;  // Controlled_Buffer controlled_buffer_210
  assign controlled_buffer_211_out = and_37_out ? out_1[9:8] : 2'bz;  // Controlled_Buffer controlled_buffer_211
  Decoder #(.select(2)) decoder_16 (
    .out0(_4RB_RS[0]), .out1(_4RB_RS[1]), .out2(_4RB_RS[2]), .out3(_4RB_RS[3]),
    .sel(controlled_buffer_211_out), .en(and_37_out));
  assign _4RB_FS = and_37_out ? 2'b01 : 2'bz;  // Controlled_Buffer controlled_buffer_212
  assign MuxASel = and_37_out ? 2'b11 : 2'bz;  // Controlled_Buffer controlled_buffer_213
  assign ALUFS = and_37_out ? 4'b0100 : 4'bz;  // Controlled_Buffer controlled_buffer_214
  assign OutBSel = and_37_out ? out_1[3:2] : 2'bz;  // Controlled_Buffer controlled_buffer_215
  assign _3RB_RS = and_37_out ? 4'b0000 : 4'bz;  // Controlled_Buffer controlled_buffer_216
  assign MuxCSel = and_37_out ? 1'b1 : 1'bz;  // Controlled_Buffer controlled_buffer_217
  assign OutASel = and_37_out ? out_1[6:5] : 2'bz;  // Controlled_Buffer controlled_buffer_218
  and and_47 (and_47_out, D3_PSH, T5);
  assign SCR = and_47_out ? 1'b1 : 1'bz;  // Controlled_Buffer controlled_buffer_219
  not not_18 (not_18_out, out_1[10]);
  and and_48 (and_48_out, D5_ADD, T4, not_18_out, not_21_out);
  assign OutDSel = and_48_out ? 2'b10 : 2'bz;  // Controlled_Buffer controlled_buffer_220
  assign MEM_SEL = and_48_out ? 1'b1 : 1'bz;  // Controlled_Buffer controlled_buffer_221
  assign MEM_LD = and_48_out ? 1'b1 : 1'bz;  // Controlled_Buffer controlled_buffer_222
  assign MuxASel = and_48_out ? 2'b01 : 2'bz;  // Controlled_Buffer controlled_buffer_223
  assign controlled_buffer_224_out = and_48_out ? out_1[9:8] : 2'bz;  // Controlled_Buffer controlled_buffer_224
  Decoder #(.select(2)) decoder_17 (
    .out0(_4RB_RS[0]), .out1(_4RB_RS[1]), .out2(_4RB_RS[2]), .out3(_4RB_RS[3]),
    .sel(controlled_buffer_224_out), .en(and_48_out));
  assign _4RB_FS = and_48_out ? 2'b01 : 2'bz;  // Controlled_Buffer controlled_buffer_225
  not not_19 (not_19_out, and_42_out);
  not not_20 (not_20_out, out_1[10]);
  and and_49 (and_49_out, D6_SUB, T4, not_20_out, not_19_out);
  assign OutDSel = and_49_out ? 2'b10 : 2'bz;  // Controlled_Buffer controlled_buffer_226
  assign MEM_SEL = and_49_out ? 1'b1 : 1'bz;  // Controlled_Buffer controlled_buffer_227
  assign MEM_LD = and_49_out ? 1'b1 : 1'bz;  // Controlled_Buffer controlled_buffer_228
  assign MuxASel = and_49_out ? 2'b01 : 2'bz;  // Controlled_Buffer controlled_buffer_229
  Decoder #(.select(2)) decoder_18 (
    .out0(_4RB_RS[0]), .out1(_4RB_RS[1]), .out2(_4RB_RS[2]), .out3(_4RB_RS[3]),
    .sel(controlled_buffer_230_out), .en(and_49_out));
  assign controlled_buffer_230_out = and_49_out ? out_1[9:8] : 2'bz;  // Controlled_Buffer controlled_buffer_230
  assign _4RB_FS = and_49_out ? 2'b01 : 2'bz;  // Controlled_Buffer controlled_buffer_231
  not not_21 (not_21_out, and_45_out);
  and and_50 (and_50_out, D4_PUL, T3);
  assign _3RB_FS = and_50_out ? 2'b10 : 2'bz;  // Controlled_Buffer controlled_buffer_232
  assign _3RB_RS = and_50_out ? 4'b0100 : 4'bz;  // Controlled_Buffer controlled_buffer_233
  assign OutDSel = and_50_out ? 2'b10 : 2'bz;  // Controlled_Buffer controlled_buffer_234
  assign MEM_SEL = and_50_out ? 1'b1 : 1'bz;  // Controlled_Buffer controlled_buffer_235
  assign MEM_LD = and_50_out ? 1'b1 : 1'bz;  // Controlled_Buffer controlled_buffer_236
  and and_51 (and_51_out, D6_SUB, T5, not_23_out);
  assign SCR = and_51_out ? 1'b1 : 1'bz;  // Controlled_Buffer controlled_buffer_237
  not not_22 (not_22_out, out_1[10]);
  and and_52 (and_52_out, D5_ADD, T5, not_22_out);
  assign SCR = and_52_out ? 1'b1 : 1'bz;  // Controlled_Buffer controlled_buffer_238
  not not_23 (not_23_out, out_1[10]);
  and and_53 (and_53_out, D4_PUL, T4, out_1[10]);
  assign MuxBSel = and_53_out ? 2'b10 : 2'bz;  // Controlled_Buffer controlled_buffer_239
  assign _3RB_FS = and_53_out ? 2'b01 : 2'bz;  // Controlled_Buffer controlled_buffer_240
  assign controlled_buffer_241_out = and_53_out ? out_1[9:8] : 2'bz;  // Controlled_Buffer controlled_buffer_241
  Decoder #(.select(2), .disabled(0)) decoder_19 (
    .out0(decoder_19_out0), .out1(decoder_19_out1), .out2(_3RB_RS[1]), .out3(_3RB_RS[2]),
    .sel(controlled_buffer_241_out), .en(and_53_out));
  or or_11 (_3RB_RS[0], decoder_19_out0, decoder_19_out1);
  not not_24 (not_24_out, out_1[10]);
  and and_54 (and_54_out, D4_PUL, T4, not_24_out);
  assign MuxASel = and_54_out ? 2'b01 : 2'bz;  // Controlled_Buffer controlled_buffer_242
  assign _4RB_FS = and_54_out ? 2'b01 : 2'bz;  // Controlled_Buffer controlled_buffer_243
  assign controlled_buffer_244_out = and_54_out ? out_1[10:8] : 3'bz;  // Controlled_Buffer controlled_buffer_244
  Decoder #(.select(3)) decoder_20 (
    .out0(_4RB_RS[0]), .out1(_4RB_RS[1]), .out2(_4RB_RS[2]), .out3(_4RB_RS[3]),
    .sel(controlled_buffer_244_out), .en(and_54_out));  // open: out4, out5, out6, out7
  and and_55 (and_55_out, D4_PUL, T5);
  assign SCR = and_55_out ? 1'b1 : 1'bz;  // Controlled_Buffer controlled_buffer_245
  assign MEM_SEL = D8_INC ? 1'b0 : 1'bz;  // Controlled_Buffer controlled_buffer_246
  assign MEM_LD = D8_INC ? 1'b0 : 1'bz;  // Controlled_Buffer controlled_buffer_247
  assign MEM_STR = D8_INC ? 1'b0 : 1'bz;  // Controlled_Buffer controlled_buffer_248
  assign MEM_CLR = D8_INC ? 1'b0 : 1'bz;  // Controlled_Buffer controlled_buffer_249
  not not_25 (not_25_out, out_1[7]);
  and and_56 (and_56_out, not_25_out, D8_INC, T3, not_27_out);
  assign MEM_SEL = D12_LSL ? 1'b0 : 1'bz;  // Controlled_Buffer controlled_buffer_250
  assign MEM_LD = D12_LSL ? 1'b0 : 1'bz;  // Controlled_Buffer controlled_buffer_251
  assign MEM_STR = D12_LSL ? 1'b0 : 1'bz;  // Controlled_Buffer controlled_buffer_252
  assign MEM_CLR = D12_LSL ? 1'b0 : 1'bz;  // Controlled_Buffer controlled_buffer_253
  and and_57 (and_57_out, D9_AND, T3, out_1[10]);
  and and_58 (and_58_out, D10_OR, T3, out_1[10]);
  and and_59 (and_59_out, and_58_out, out_1[4]);
  assign OutASel = and_56_out ? out_1[6:5] : 2'bz;  // Controlled_Buffer controlled_buffer_254
  assign MuxCSel = and_56_out ? 1'b1 : 1'bz;  // Controlled_Buffer controlled_buffer_255
  assign ALUFS = and_56_out ? 4'b0000 : 4'bz;  // Controlled_Buffer controlled_buffer_256
  assign MuxASel = and_56_out ? 2'b11 : 2'bz;  // Controlled_Buffer controlled_buffer_257
  assign controlled_buffer_258_out = and_56_out ? out_1[10:8] : 3'bz;  // Controlled_Buffer controlled_buffer_258
  Decoder #(.select(3)) decoder_21 (
    .out0(_4RB_RS[0]), .out1(_4RB_RS[1]), .out2(_4RB_RS[2]), .out3(_4RB_RS[3]),
    .sel(controlled_buffer_258_out), .en(and_56_out));  // open: out4, out5, out6, out7
  assign _4RB_FS = and_56_out ? 2'b01 : 2'bz;  // Controlled_Buffer controlled_buffer_259
  and and_60 (and_60_out, out_1[7], D8_INC, T3, not_28_out);
  outcdecoder outcdecoder_12 (.in_1(controlled_buffer_260_out), .out_2(OutCSel));
  assign controlled_buffer_260_out = and_60_out ? out_1[6:5] : 2'bz;  // Controlled_Buffer controlled_buffer_260
  assign MuxASel = and_60_out ? 2'b10 : 2'bz;  // Controlled_Buffer controlled_buffer_261
  assign MuxCSel = and_60_out ? 1'b0 : 1'bz;  // Controlled_Buffer controlled_buffer_262
  assign _4RB_FS = and_60_out ? 2'b01 : 2'bz;  // Controlled_Buffer controlled_buffer_263
  Decoder #(.select(3)) decoder_22 (
    .out0(_4RB_RS[0]), .out1(_4RB_RS[1]), .out2(_4RB_RS[2]), .out3(_4RB_RS[3]),
    .sel(controlled_buffer_264_out), .en(and_60_out));  // open: out4, out5, out6, out7
  assign controlled_buffer_264_out = and_60_out ? out_1[10:8] : 3'bz;  // Controlled_Buffer controlled_buffer_264
  assign _4RB_FS = and_60_out ? 2'b01 : 2'bz;  // Controlled_Buffer controlled_buffer_265
  and and_61 (and_61_out, out_1[7], D12_LSL, T3, not_34_out);
  and and_62 (and_62_out, and_57_out, out_1[7]);
  and and_63 (and_63_out, and_57_out, out_1[4]);
  and and_64 (and_64_out, and_58_out, out_1[7]);
  not not_26 (not_26_out, out_1[4]);
  not not_27 (not_27_out, out_1[10]);
  not not_28 (not_28_out, out_1[10]);
  not not_29 (not_29_out, out_1[7]);
  outcdecoder outcdecoder_13 (.in_1(controlled_buffer_266_out), .out_2(OutCSel));
  assign controlled_buffer_266_out = and_61_out ? out_1[6:5] : 2'bz;  // Controlled_Buffer controlled_buffer_266
  assign MuxASel = and_61_out ? 2'b10 : 2'bz;  // Controlled_Buffer controlled_buffer_267
  assign MuxCSel = and_61_out ? 1'b0 : 1'bz;  // Controlled_Buffer controlled_buffer_268
  assign _4RB_FS = and_61_out ? 2'b01 : 2'bz;  // Controlled_Buffer controlled_buffer_269
  Decoder #(.select(3)) decoder_23 (
    .out0(_4RB_RS[0]), .out1(_4RB_RS[1]), .out2(_4RB_RS[2]), .out3(_4RB_RS[3]),
    .sel(controlled_buffer_270_out), .en(and_61_out));  // open: out4, out5, out6, out7
  assign controlled_buffer_270_out = and_61_out ? out_1[10:8] : 3'bz;  // Controlled_Buffer controlled_buffer_270
  assign _4RB_FS = and_61_out ? 2'b01 : 2'bz;  // Controlled_Buffer controlled_buffer_271
  not not_30 (not_30_out, out_1[7]);
  not not_31 (not_31_out, out_1[4]);
  and and_65 (and_65_out, and_58_out, not_32_out, not_26_out);
  not not_32 (not_32_out, out_1[7]);
  not not_33 (not_33_out, out_1[7]);
  not not_34 (not_34_out, out_1[10]);
  outcdecoder outcdecoder_14 (.in_1(out_1[6:5]), .out_2(outcdecoder_14_out_2));
  and and_66 (and_66_out, and_57_out, not_30_out, not_31_out);
  outcdecoder outcdecoder_15 (.in_1(out_1[3:2]), .out_2(outcdecoder_15_out_2));
  Decoder #(.select(2), .disabled(0)) decoder_24 (
    .out0(decoder_24_out0), .out1(decoder_24_out1), .out2(_3RB_RS[1]), .out3(_3RB_RS[2]),
    .sel(controlled_buffer_272_out), .en(and_64_out));
  assign controlled_buffer_272_out = and_64_out ? out_1[9:8] : 2'bz;  // Controlled_Buffer controlled_buffer_272
  or or_12 (_3RB_RS[0], decoder_24_out0, decoder_24_out1);
  assign _3RB_FS = and_64_out ? 2'b01 : 2'bz;  // Controlled_Buffer controlled_buffer_273
  assign MuxBSel = and_64_out ? 2'b11 : 2'bz;  // Controlled_Buffer controlled_buffer_274
  assign ALUFS = and_64_out ? 4'b1000 : 4'bz;  // Controlled_Buffer controlled_buffer_275
  assign MuxASel = and_64_out ? 2'b10 : 2'bz;  // Controlled_Buffer controlled_buffer_276
  assign OutBSel = and_64_out ? out_1[3:2] : 2'bz;  // Controlled_Buffer controlled_buffer_277
  assign OutCSel = and_64_out ? outcdecoder_16_out_2 : 2'bz;  // Controlled_Buffer controlled_buffer_278
  outcdecoder outcdecoder_16 (.in_1(out_1[6:5]), .out_2(outcdecoder_16_out_2));
  assign MuxCSel = and_64_out ? 1'b0 : 1'bz;  // Controlled_Buffer controlled_buffer_279
  assign controlled_buffer_280_out = and_59_out ? out_1[9:8] : 2'bz;  // Controlled_Buffer controlled_buffer_280
  Decoder #(.select(2), .disabled(0)) decoder_25 (
    .out0(decoder_25_out0), .out1(decoder_25_out1), .out2(_3RB_RS[1]), .out3(_3RB_RS[2]),
    .sel(controlled_buffer_280_out), .en(and_59_out));
  or or_13 (_3RB_RS[0], decoder_25_out0, decoder_25_out1);
  assign _3RB_FS = and_59_out ? 2'b01 : 2'bz;  // Controlled_Buffer controlled_buffer_281
  assign MuxBSel = and_59_out ? 2'b11 : 2'bz;  // Controlled_Buffer controlled_buffer_282
  assign ALUFS = and_59_out ? 4'b1000 : 4'bz;  // Controlled_Buffer controlled_buffer_283
  assign MuxASel = and_59_out ? 2'b10 : 2'bz;  // Controlled_Buffer controlled_buffer_284
  assign OutBSel = and_59_out ? out_1[6:5] : 2'bz;  // Controlled_Buffer controlled_buffer_285
  outcdecoder outcdecoder_17 (.in_1(out_1[3:2]), .out_2(outcdecoder_17_out_2));
  assign OutCSel = and_59_out ? outcdecoder_17_out_2 : 2'bz;  // Controlled_Buffer controlled_buffer_286
  assign MuxCSel = and_59_out ? 1'b0 : 1'bz;  // Controlled_Buffer controlled_buffer_287
  and and_67 (and_67_out, not_33_out, D8_INC, T4, not_35_out);
  assign _4RB_FS = and_67_out ? 2'b10 : 2'bz;  // Controlled_Buffer controlled_buffer_288
  assign controlled_buffer_289_out = and_67_out ? out_1[10:8] : 3'bz;  // Controlled_Buffer controlled_buffer_289
  and and_68 (and_68_out, out_1[7], D8_INC, T4, not_37_out);
  assign _4RB_FS = and_68_out ? 2'b10 : 2'bz;  // Controlled_Buffer controlled_buffer_290
  assign controlled_buffer_291_out = and_68_out ? out_1[10:8] : 3'bz;  // Controlled_Buffer controlled_buffer_291
  and and_69 (and_69_out, not_29_out, D12_LSL, T3, not_36_out);
  assign OutASel = and_69_out ? out_1[6:5] : 2'bz;  // Controlled_Buffer controlled_buffer_292
  assign MuxCSel = and_69_out ? 1'b1 : 1'bz;  // Controlled_Buffer controlled_buffer_293
  assign ALUFS = and_69_out ? 4'b1010 : 4'bz;  // Controlled_Buffer controlled_buffer_294
  assign MuxASel = and_69_out ? 2'b11 : 2'bz;  // Controlled_Buffer controlled_buffer_295
  assign controlled_buffer_296_out = and_69_out ? out_1[10:8] : 3'bz;  // Controlled_Buffer controlled_buffer_296
  Decoder #(.select(3)) decoder_26 (
    .out0(_4RB_RS[0]), .out1(_4RB_RS[1]), .out2(_4RB_RS[2]), .out3(_4RB_RS[3]),
    .sel(controlled_buffer_296_out), .en(and_69_out));  // open: out4, out5, out6, out7
  assign _4RB_FS = and_69_out ? 2'b01 : 2'bz;  // Controlled_Buffer controlled_buffer_297
  assign controlled_buffer_298_out = and_62_out ? out_1[9:8] : 2'bz;  // Controlled_Buffer controlled_buffer_298
  Decoder #(.select(2), .disabled(0)) decoder_27 (
    .out0(decoder_27_out0), .out1(decoder_27_out1), .out2(_3RB_RS[1]), .out3(_3RB_RS[2]),
    .sel(controlled_buffer_298_out), .en(and_62_out));
  or or_14 (_3RB_RS[0], decoder_27_out0, decoder_27_out1);
  assign _3RB_FS = and_62_out ? 2'b01 : 2'bz;  // Controlled_Buffer controlled_buffer_299
  assign MuxBSel = and_62_out ? 2'b11 : 2'bz;  // Controlled_Buffer controlled_buffer_300
  assign ALUFS = and_62_out ? 4'b0111 : 4'bz;  // Controlled_Buffer controlled_buffer_301
  assign MuxASel = and_62_out ? 2'b10 : 2'bz;  // Controlled_Buffer controlled_buffer_302
  assign OutBSel = and_62_out ? out_1[3:2] : 2'bz;  // Controlled_Buffer controlled_buffer_303
  assign OutCSel = and_62_out ? outcdecoder_14_out_2 : 2'bz;  // Controlled_Buffer controlled_buffer_304
  assign MuxCSel = and_62_out ? 1'b0 : 1'bz;  // Controlled_Buffer controlled_buffer_305
  Decoder #(.select(2), .disabled(0)) decoder_28 (
    .out0(decoder_28_out0), .out1(decoder_28_out1), .out2(_3RB_RS[1]), .out3(_3RB_RS[2]),
    .sel(controlled_buffer_306_out), .en(and_63_out));
  assign controlled_buffer_306_out = and_63_out ? out_1[9:8] : 2'bz;  // Controlled_Buffer controlled_buffer_306
  or or_15 (_3RB_RS[0], decoder_28_out0, decoder_28_out1);
  assign _3RB_FS = and_63_out ? 2'b01 : 2'bz;  // Controlled_Buffer controlled_buffer_307
  assign MuxBSel = and_63_out ? 2'b11 : 2'bz;  // Controlled_Buffer controlled_buffer_308
  assign ALUFS = and_63_out ? 4'b0111 : 4'bz;  // Controlled_Buffer controlled_buffer_309
  assign MuxASel = and_63_out ? 2'b10 : 2'bz;  // Controlled_Buffer controlled_buffer_310
  assign OutBSel = and_63_out ? out_1[6:5] : 2'bz;  // Controlled_Buffer controlled_buffer_311
  assign OutCSel = and_63_out ? outcdecoder_15_out_2 : 2'bz;  // Controlled_Buffer controlled_buffer_312
  assign MuxCSel = and_63_out ? 1'b0 : 1'bz;  // Controlled_Buffer controlled_buffer_313
  not not_35 (not_35_out, out_1[10]);
  Decoder #(.select(3)) decoder_29 (
    .out0(_4RB_RS[0]), .out1(_4RB_RS[1]), .out2(_4RB_RS[2]), .out3(_4RB_RS[3]),
    .sel(controlled_buffer_289_out), .en(and_67_out));  // open: out4, out5, out6, out7
  Decoder #(.select(3)) decoder_30 (
    .out0(_4RB_RS[0]), .out1(_4RB_RS[1]), .out2(_4RB_RS[2]), .out3(_4RB_RS[3]),
    .sel(controlled_buffer_291_out), .en(and_68_out));  // open: out4, out5, out6, out7
  not not_36 (not_36_out, out_1[10]);
  and and_70 (and_70_out, out_1[7], D12_LSL, T4, not_38_out);
  assign OutASel = and_70_out ? out_1[9:8] : 2'bz;  // Controlled_Buffer controlled_buffer_314
  assign MuxCSel = and_70_out ? 1'b1 : 1'bz;  // Controlled_Buffer controlled_buffer_315
  assign ALUFS = and_70_out ? 4'b1010 : 4'bz;  // Controlled_Buffer controlled_buffer_316
  assign MuxASel = and_70_out ? 2'b11 : 2'bz;  // Controlled_Buffer controlled_buffer_317
  assign controlled_buffer_318_out = and_70_out ? out_1[10:8] : 3'bz;  // Controlled_Buffer controlled_buffer_318
  assign _4RB_FS = and_70_out ? 2'b01 : 2'bz;  // Controlled_Buffer controlled_buffer_319
  not not_37 (not_37_out, out_1[10]);
  not not_38 (not_38_out, out_1[10]);
  Decoder #(.select(3)) decoder_31 (
    .out0(_4RB_RS[0]), .out1(_4RB_RS[1]), .out2(_4RB_RS[2]), .out3(_4RB_RS[3]),
    .sel(controlled_buffer_318_out), .en(and_70_out));  // open: out4, out5, out6, out7
  and and_71 (and_71_out, D9_AND, T4, out_1[10]);
  assign SCR = and_71_out ? 1'b1 : 1'bz;  // Controlled_Buffer controlled_buffer_320
  and and_72 (and_72_out, D10_OR, T4, out_1[10]);
  assign SCR = and_72_out ? 1'b1 : 1'bz;  // Controlled_Buffer controlled_buffer_321
  not not_39 (not_39_out, out_1[7]);
  assign controlled_buffer_322_out = and_65_out ? out_1[9:8] : 2'bz;  // Controlled_Buffer controlled_buffer_322
  assign _3RB_FS = and_65_out ? 2'b01 : 2'bz;  // Controlled_Buffer controlled_buffer_323
  assign MuxBSel = and_65_out ? 2'b11 : 2'bz;  // Controlled_Buffer controlled_buffer_324
  assign ALUFS = and_65_out ? 4'b1000 : 4'bz;  // Controlled_Buffer controlled_buffer_325
  assign OutBSel = and_65_out ? out_1[3:2] : 2'bz;  // Controlled_Buffer controlled_buffer_326
  assign MuxCSel = and_65_out ? 1'b1 : 1'bz;  // Controlled_Buffer controlled_buffer_327
  assign OutASel = and_65_out ? out_1[6:5] : 2'bz;  // Controlled_Buffer controlled_buffer_328
  and and_73 (and_73_out, out_1[7], D8_INC, T3, out_1[10]);
  not not_40 (not_40_out, out_1[7]);
  Decoder #(.select(2), .disabled(0)) decoder_32 (
    .out0(decoder_32_out0), .out1(decoder_32_out1), .out2(_3RB_RS[1]), .out3(_3RB_RS[2]),
    .sel(controlled_buffer_329_out), .en(and_66_out));
  assign controlled_buffer_329_out = and_66_out ? out_1[9:8] : 2'bz;  // Controlled_Buffer controlled_buffer_329
  or or_16 (_3RB_RS[0], decoder_32_out0, decoder_32_out1);
  assign _3RB_FS = and_66_out ? 2'b01 : 2'bz;  // Controlled_Buffer controlled_buffer_330
  assign MuxBSel = and_66_out ? 2'b11 : 2'bz;  // Controlled_Buffer controlled_buffer_331
  assign ALUFS = and_66_out ? 4'b0111 : 4'bz;  // Controlled_Buffer controlled_buffer_332
  assign OutBSel = and_66_out ? out_1[3:2] : 2'bz;  // Controlled_Buffer controlled_buffer_333
  assign MuxCSel = and_66_out ? 1'b1 : 1'bz;  // Controlled_Buffer controlled_buffer_334
  assign OutASel = and_66_out ? out_1[6:5] : 2'bz;  // Controlled_Buffer controlled_buffer_335
  Decoder #(.select(2), .disabled(0)) decoder_33 (
    .out0(decoder_33_out0), .out1(decoder_33_out1), .out2(_3RB_RS[1]), .out3(_3RB_RS[2]),
    .sel(controlled_buffer_322_out), .en(and_65_out));
  or or_17 (_3RB_RS[0], decoder_33_out0, decoder_33_out1);
  assign controlled_buffer_336_out = and_73_out ? out_1[6:5] : 2'bz;  // Controlled_Buffer controlled_buffer_336
  outcdecoder outcdecoder_18 (.in_1(controlled_buffer_336_out), .out_2(OutCSel));
  assign MuxASel = and_73_out ? 2'b10 : 2'bz;  // Controlled_Buffer controlled_buffer_337
  assign MuxCSel = and_73_out ? 1'b0 : 1'bz;  // Controlled_Buffer controlled_buffer_338
  assign ALUFS = and_73_out ? 4'b0000 : 4'bz;  // Controlled_Buffer controlled_buffer_339
  assign MuxBSel = and_73_out ? 2'b11 : 2'bz;  // Controlled_Buffer controlled_buffer_340
  assign _3RB_FS = and_73_out ? 2'b01 : 2'bz;  // Controlled_Buffer controlled_buffer_341
  Decoder #(.select(2), .disabled(0)) decoder_34 (
    .out0(decoder_34_out0), .out1(decoder_34_out1), .out2(_3RB_RS[1]), .out3(_3RB_RS[2]),
    .sel(controlled_buffer_342_out), .en(and_73_out));
  assign controlled_buffer_342_out = and_73_out ? out_1[9:8] : 2'bz;  // Controlled_Buffer controlled_buffer_342
  or or_18 (_3RB_RS[0], decoder_34_out0, decoder_34_out1);
  and and_74 (and_74_out, not_39_out, D8_INC, T3, out_1[10]);
  assign OutASel = and_74_out ? out_1[6:5] : 2'bz;  // Controlled_Buffer controlled_buffer_343
  assign MuxCSel = and_74_out ? 1'b1 : 1'bz;  // Controlled_Buffer controlled_buffer_344
  assign ALUFS = and_74_out ? 4'b0000 : 4'bz;  // Controlled_Buffer controlled_buffer_345
  assign MuxBSel = and_74_out ? 2'b11 : 2'bz;  // Controlled_Buffer controlled_buffer_346
  assign controlled_buffer_347_out = and_74_out ? out_1[9:8] : 2'bz;  // Controlled_Buffer controlled_buffer_347
  Decoder #(.select(2), .disabled(0)) decoder_35 (
    .out0(decoder_35_out0), .out1(decoder_35_out1), .out2(_3RB_RS[1]), .out3(_3RB_RS[2]),
    .sel(controlled_buffer_347_out), .en(and_74_out));
  or or_19 (_3RB_RS[0], decoder_35_out0, decoder_35_out1);
  assign _3RB_FS = and_74_out ? 2'b01 : 2'bz;  // Controlled_Buffer controlled_buffer_348
  and and_75 (and_75_out, out_1[7], D12_LSL, T3, out_1[10]);
  assign controlled_buffer_349_out = and_75_out ? out_1[6:5] : 2'bz;  // Controlled_Buffer controlled_buffer_349
  outcdecoder outcdecoder_19 (.in_1(controlled_buffer_349_out), .out_2(OutCSel));
  assign MuxASel = and_75_out ? 2'b10 : 2'bz;  // Controlled_Buffer controlled_buffer_350
  assign MuxCSel = and_75_out ? 1'b0 : 1'bz;  // Controlled_Buffer controlled_buffer_351
  assign ALUFS = and_75_out ? 4'b1010 : 4'bz;  // Controlled_Buffer controlled_buffer_352
  assign MuxBSel = and_75_out ? 2'b11 : 2'bz;  // Controlled_Buffer controlled_buffer_353
  assign _3RB_FS = and_75_out ? 2'b01 : 2'bz;  // Controlled_Buffer controlled_buffer_354
  Decoder #(.select(2), .disabled(0)) decoder_36 (
    .out0(decoder_36_out0), .out1(decoder_36_out1), .out2(_3RB_RS[1]), .out3(_3RB_RS[2]),
    .sel(controlled_buffer_355_out), .en(and_75_out));
  assign controlled_buffer_355_out = and_75_out ? out_1[9:8] : 2'bz;  // Controlled_Buffer controlled_buffer_355
  or or_20 (_3RB_RS[0], decoder_36_out0, decoder_36_out1);
  and and_76 (and_76_out, not_40_out, D12_LSL, T3, out_1[10]);
  assign OutASel = and_76_out ? out_1[6:5] : 2'bz;  // Controlled_Buffer controlled_buffer_356
  assign MuxCSel = and_76_out ? 1'b1 : 1'bz;  // Controlled_Buffer controlled_buffer_357
  assign ALUFS = and_76_out ? 4'b1010 : 4'bz;  // Controlled_Buffer controlled_buffer_358
  assign MuxBSel = and_76_out ? 2'b11 : 2'bz;  // Controlled_Buffer controlled_buffer_359
  assign controlled_buffer_360_out = and_76_out ? out_1[9:8] : 2'bz;  // Controlled_Buffer controlled_buffer_360
  Decoder #(.select(2), .disabled(0)) decoder_37 (
    .out0(decoder_37_out0), .out1(decoder_37_out1), .out2(_3RB_RS[1]), .out3(_3RB_RS[2]),
    .sel(controlled_buffer_360_out), .en(and_76_out));
  or or_21 (_3RB_RS[0], decoder_37_out0, decoder_37_out1);
  assign _3RB_FS = and_76_out ? 2'b01 : 2'bz;  // Controlled_Buffer controlled_buffer_361
  not not_41 (not_41_out, out_1[7]);
  and and_77 (and_77_out, out_1[7], D8_INC, T4, out_1[10]);
  assign _3RB_FS = and_77_out ? 2'b10 : 2'bz;  // Controlled_Buffer controlled_buffer_362
  assign controlled_buffer_363_out = and_77_out ? out_1[9:8] : 2'bz;  // Controlled_Buffer controlled_buffer_363
  and and_78 (and_78_out, not_41_out, D8_INC, T4, out_1[10]);
  assign _3RB_FS = and_78_out ? 2'b10 : 2'bz;  // Controlled_Buffer controlled_buffer_364
  assign controlled_buffer_365_out = and_78_out ? out_1[9:8] : 2'bz;  // Controlled_Buffer controlled_buffer_365
  not not_42 (not_42_out, out_1[7]);
  Decoder #(.select(2), .disabled(0)) decoder_38 (
    .out0(decoder_38_out0), .out1(decoder_38_out1), .out2(_3RB_RS[1]), .out3(_3RB_RS[2]),
    .sel(controlled_buffer_363_out), .en(and_77_out));
  or or_22 (_3RB_RS[0], decoder_38_out0, decoder_38_out1);
  Decoder #(.select(2), .disabled(0)) decoder_39 (
    .out0(decoder_39_out0), .out1(decoder_39_out1), .out2(_3RB_RS[1]), .out3(_3RB_RS[2]),
    .sel(controlled_buffer_365_out), .en(and_78_out));
  or or_23 (_3RB_RS[0], decoder_39_out0, decoder_39_out1);
  and and_79 (and_79_out, out_1[7], out_1[10]);
  or or_24 (or_24_out, not_42_out, and_79_out);
  and and_80 (and_80_out, or_24_out, D12_LSL, T4);
  not not_43 (not_43_out, out_1[10]);
  and and_81 (and_81_out, D10_OR, T3, not_43_out);
  assign SCR = and_80_out ? 1'b1 : 1'bz;  // Controlled_Buffer controlled_buffer_366
  and and_82 (and_82_out, out_1[7], D12_LSL, T5, not_45_out);
  assign SCR = and_82_out ? 1'b1 : 1'bz;  // Controlled_Buffer controlled_buffer_367
  not not_44 (not_44_out, out_1[10]);
  and and_83 (and_83_out, D9_AND, T3, not_44_out);
  and and_84 (and_84_out, and_83_out, out_1[4]);
  and and_85 (and_85_out, and_81_out, out_1[7]);
  and and_86 (and_86_out, and_81_out, out_1[4]);
  and and_87 (and_87_out, D8_INC, T6);
  assign SCR = and_87_out ? 1'b1 : 1'bz;  // Controlled_Buffer controlled_buffer_368
  not not_45 (not_45_out, out_1[10]);
  and and_88 (and_88_out, and_83_out, out_1[7]);
  not not_46 (not_46_out, out_1[4]);
  not not_47 (not_47_out, out_1[7]);
  not not_48 (not_48_out, out_1[4]);
  not not_49 (not_49_out, out_1[10]);
  and and_89 (and_89_out, D8_INC, T5, not_49_out);
  assign _4RB_RS = and_89_out ? 4'b0000 : 4'bz;  // Controlled_Buffer controlled_buffer_369
  assign OutASel = and_89_out ? out_1[9:8] : 2'bz;  // Controlled_Buffer controlled_buffer_370
  assign MuxCSel = and_89_out ? 1'b1 : 1'bz;  // Controlled_Buffer controlled_buffer_371
  and and_90 (and_90_out, D8_INC, T5, out_1[10]);
  assign _3RB_RS = and_90_out ? 4'b0000 : 4'bz;  // Controlled_Buffer controlled_buffer_372
  assign controlled_buffer_373_out = and_90_out ? out_1[9:8] : 2'bz;  // Controlled_Buffer controlled_buffer_373
  outcdecoder outcdecoder_20 (.in_1(controlled_buffer_373_out), .out_2(OutCSel));
  assign MuxASel = and_90_out ? 2'b11 : 2'bz;  // Controlled_Buffer controlled_buffer_374
  assign _4RB_RS = and_90_out ? 4'b0000 : 4'bz;  // Controlled_Buffer controlled_buffer_375
  assign MuxCSel = and_90_out ? 1'b0 : 1'bz;  // Controlled_Buffer controlled_buffer_376
  and and_91 (and_91_out, and_83_out, not_50_out, not_46_out);
  not not_50 (not_50_out, out_1[7]);
  outcdecoder outcdecoder_21 (.in_1(out_1[6:5]), .out_2(outcdecoder_21_out_2));
  and and_92 (and_92_out, and_81_out, not_47_out, not_48_out);
  outcdecoder outcdecoder_22 (.in_1(out_1[3:2]), .out_2(outcdecoder_22_out_2));
  or or_25 (or_25_out, D8_INC, D7_DEC);
  assign ALUFS = or_25_out ? 4'b0000 : 4'bz;  // Controlled_Buffer controlled_buffer_377
  assign MEM_SEL = and_88_out ? 1'b1 : 1'bz;  // Controlled_Buffer controlled_buffer_378
  assign MEM_LD = and_88_out ? 1'b1 : 1'bz;  // Controlled_Buffer controlled_buffer_379
  assign MEM_STR = and_88_out ? 1'b1 : 1'bz;  // Controlled_Buffer controlled_buffer_380
  assign ALUFS = and_88_out ? 4'b0111 : 4'bz;  // Controlled_Buffer controlled_buffer_381
  assign MuxASel = and_88_out ? 2'b10 : 2'bz;  // Controlled_Buffer controlled_buffer_382
  assign OutBSel = and_88_out ? out_1[3:2] : 2'bz;  // Controlled_Buffer controlled_buffer_383
  assign OutCSel = and_88_out ? outcdecoder_23_out_2 : 2'bz;  // Controlled_Buffer controlled_buffer_384
  outcdecoder outcdecoder_23 (.in_1(out_1[6:5]), .out_2(outcdecoder_23_out_2));
  assign MuxCSel = and_88_out ? 1'b0 : 1'bz;  // Controlled_Buffer controlled_buffer_385
  assign OutDSel = and_88_out ? 2'b10 : 2'bz;  // Controlled_Buffer controlled_buffer_386
  assign MEM_SEL = and_84_out ? 1'b1 : 1'bz;  // Controlled_Buffer controlled_buffer_387
  assign MEM_LD = and_84_out ? 1'b1 : 1'bz;  // Controlled_Buffer controlled_buffer_388
  assign MEM_STR = and_84_out ? 1'b1 : 1'bz;  // Controlled_Buffer controlled_buffer_389
  assign ALUFS = and_84_out ? 4'b0111 : 4'bz;  // Controlled_Buffer controlled_buffer_390
  assign MuxASel = and_84_out ? 2'b10 : 2'bz;  // Controlled_Buffer controlled_buffer_391
  assign OutBSel = and_84_out ? out_1[6:5] : 2'bz;  // Controlled_Buffer controlled_buffer_392
  outcdecoder outcdecoder_24 (.in_1(out_1[3:2]), .out_2(outcdecoder_24_out_2));
  assign OutCSel = and_84_out ? outcdecoder_24_out_2 : 2'bz;  // Controlled_Buffer controlled_buffer_393
  assign MuxCSel = and_84_out ? 1'b0 : 1'bz;  // Controlled_Buffer controlled_buffer_394
  assign OutDSel = and_84_out ? 2'b10 : 2'bz;  // Controlled_Buffer controlled_buffer_395
  assign MEM_SEL = and_85_out ? 1'b1 : 1'bz;  // Controlled_Buffer controlled_buffer_396
  assign MEM_LD = and_85_out ? 1'b1 : 1'bz;  // Controlled_Buffer controlled_buffer_397
  assign MEM_STR = and_85_out ? 1'b1 : 1'bz;  // Controlled_Buffer controlled_buffer_398
  assign ALUFS = and_85_out ? 4'b1000 : 4'bz;  // Controlled_Buffer controlled_buffer_399
  assign MuxASel = and_85_out ? 2'b10 : 2'bz;  // Controlled_Buffer controlled_buffer_400
  assign OutBSel = and_85_out ? out_1[3:2] : 2'bz;  // Controlled_Buffer controlled_buffer_401
  assign OutCSel = and_85_out ? outcdecoder_21_out_2 : 2'bz;  // Controlled_Buffer controlled_buffer_402
  assign MuxCSel = and_85_out ? 1'b0 : 1'bz;  // Controlled_Buffer controlled_buffer_403
  assign OutDSel = and_85_out ? 2'b10 : 2'bz;  // Controlled_Buffer controlled_buffer_404
  and and_93 (and_93_out, not_47_out, not_48_out);
  assign MEM_SEL = and_86_out ? 1'b1 : 1'bz;  // Controlled_Buffer controlled_buffer_405
  assign MEM_LD = and_86_out ? 1'b1 : 1'bz;  // Controlled_Buffer controlled_buffer_406
  assign MEM_STR = and_86_out ? 1'b1 : 1'bz;  // Controlled_Buffer controlled_buffer_407
  assign ALUFS = and_86_out ? 4'b1000 : 4'bz;  // Controlled_Buffer controlled_buffer_408
  assign MuxASel = and_86_out ? 2'b10 : 2'bz;  // Controlled_Buffer controlled_buffer_409
  assign OutBSel = and_86_out ? out_1[6:5] : 2'bz;  // Controlled_Buffer controlled_buffer_410
  assign OutCSel = and_86_out ? outcdecoder_22_out_2 : 2'bz;  // Controlled_Buffer controlled_buffer_411
  assign MuxCSel = and_86_out ? 1'b0 : 1'bz;  // Controlled_Buffer controlled_buffer_412
  assign OutDSel = and_86_out ? 2'b10 : 2'bz;  // Controlled_Buffer controlled_buffer_413
  and and_94 (and_94_out, not_50_out, not_46_out);
  assign MEM_SEL = D13_LSR ? 1'b0 : 1'bz;  // Controlled_Buffer controlled_buffer_414
  assign MEM_LD = D13_LSR ? 1'b0 : 1'bz;  // Controlled_Buffer controlled_buffer_415
  assign MEM_STR = D13_LSR ? 1'b0 : 1'bz;  // Controlled_Buffer controlled_buffer_416
  assign MEM_CLR = D13_LSR ? 1'b0 : 1'bz;  // Controlled_Buffer controlled_buffer_417
  assign MEM_SEL = D7_DEC ? 1'b0 : 1'bz;  // Controlled_Buffer controlled_buffer_418
  assign MEM_LD = D7_DEC ? 1'b0 : 1'bz;  // Controlled_Buffer controlled_buffer_419
  assign MEM_STR = D7_DEC ? 1'b0 : 1'bz;  // Controlled_Buffer controlled_buffer_420
  assign MEM_CLR = D7_DEC ? 1'b0 : 1'bz;  // Controlled_Buffer controlled_buffer_421
  assign controlled_buffer_422_out = and_92_out ? out_1[9:8] : 2'bz;  // Controlled_Buffer controlled_buffer_422
  Decoder #(.select(2)) decoder_40 (
    .out0(_4RB_RS[0]), .out1(_4RB_RS[1]), .out2(_4RB_RS[2]), .out3(_4RB_RS[3]),
    .sel(controlled_buffer_422_out), .en(and_92_out));
  assign _4RB_FS = and_92_out ? 2'b01 : 2'bz;  // Controlled_Buffer controlled_buffer_423
  assign MuxASel = and_92_out ? 2'b11 : 2'bz;  // Controlled_Buffer controlled_buffer_424
  assign ALUFS = and_92_out ? 4'b1000 : 4'bz;  // Controlled_Buffer controlled_buffer_425
  assign OutBSel = and_92_out ? out_1[3:2] : 2'bz;  // Controlled_Buffer controlled_buffer_426
  assign _3RB_RS = and_92_out ? 4'b0000 : 4'bz;  // Controlled_Buffer controlled_buffer_427
  assign MuxCSel = and_92_out ? 1'b1 : 1'bz;  // Controlled_Buffer controlled_buffer_428
  assign OutASel = and_92_out ? out_1[6:5] : 2'bz;  // Controlled_Buffer controlled_buffer_429
  not not_51 (not_51_out, out_1[7]);
  and and_95 (and_95_out, out_1[7], D13_LSR, T3, not_53_out);
  assign controlled_buffer_430_out = and_95_out ? out_1[6:5] : 2'bz;  // Controlled_Buffer controlled_buffer_430
  assign MuxASel = and_95_out ? 2'b10 : 2'bz;  // Controlled_Buffer controlled_buffer_431
  assign MuxCSel = and_95_out ? 1'b0 : 1'bz;  // Controlled_Buffer controlled_buffer_432
  assign _4RB_FS = and_95_out ? 2'b01 : 2'bz;  // Controlled_Buffer controlled_buffer_433
  assign controlled_buffer_434_out = and_95_out ? out_1[10:8] : 3'bz;  // Controlled_Buffer controlled_buffer_434
  Decoder #(.select(3)) decoder_41 (
    .out0(_4RB_RS[0]), .out1(_4RB_RS[1]), .out2(_4RB_RS[2]), .out3(_4RB_RS[3]),
    .sel(controlled_buffer_434_out), .en(and_95_out));  // open: out4, out5, out6, out7
  assign _4RB_FS = and_95_out ? 2'b01 : 2'bz;  // Controlled_Buffer controlled_buffer_435
  Decoder #(.select(2)) decoder_42 (
    .out0(_4RB_RS[0]), .out1(_4RB_RS[1]), .out2(_4RB_RS[2]), .out3(_4RB_RS[3]),
    .sel(controlled_buffer_436_out), .en(and_91_out));
  assign controlled_buffer_436_out = and_91_out ? out_1[9:8] : 2'bz;  // Controlled_Buffer controlled_buffer_436
  assign _4RB_FS = and_91_out ? 2'b01 : 2'bz;  // Controlled_Buffer controlled_buffer_437
  assign MuxASel = and_91_out ? 2'b11 : 2'bz;  // Controlled_Buffer controlled_buffer_438
  assign ALUFS = and_91_out ? 4'b0111 : 4'bz;  // Controlled_Buffer controlled_buffer_439
  assign OutBSel = and_91_out ? out_1[3:2] : 2'bz;  // Controlled_Buffer controlled_buffer_440
  assign _3RB_RS = and_91_out ? 4'b0000 : 4'bz;  // Controlled_Buffer controlled_buffer_441
  assign MuxCSel = and_91_out ? 1'b1 : 1'bz;  // Controlled_Buffer controlled_buffer_442
  assign OutASel = and_91_out ? out_1[6:5] : 2'bz;  // Controlled_Buffer controlled_buffer_443
  not not_52 (not_52_out, out_1[7]);
  not not_53 (not_53_out, out_1[10]);
  outcdecoder outcdecoder_25 (.in_1(controlled_buffer_430_out), .out_2(OutCSel));
  and and_96 (and_96_out, not_52_out, D7_DEC, T3, not_54_out);
  assign OutASel = and_96_out ? out_1[6:5] : 2'bz;  // Controlled_Buffer controlled_buffer_444
  assign MuxCSel = and_96_out ? 1'b1 : 1'bz;  // Controlled_Buffer controlled_buffer_445
  assign ALUFS = and_96_out ? 4'b0000 : 4'bz;  // Controlled_Buffer controlled_buffer_446
  assign MuxASel = and_96_out ? 2'b11 : 2'bz;  // Controlled_Buffer controlled_buffer_447
  assign controlled_buffer_448_out = and_96_out ? out_1[10:8] : 3'bz;  // Controlled_Buffer controlled_buffer_448
  assign _4RB_FS = and_96_out ? 2'b01 : 2'bz;  // Controlled_Buffer controlled_buffer_449
  and and_97 (and_97_out, out_1[7], D7_DEC, T3, not_55_out);
  assign controlled_buffer_450_out = and_97_out ? out_1[6:5] : 2'bz;  // Controlled_Buffer controlled_buffer_450
  assign MuxASel = and_97_out ? 2'b10 : 2'bz;  // Controlled_Buffer controlled_buffer_451
  assign MuxCSel = and_97_out ? 1'b0 : 1'bz;  // Controlled_Buffer controlled_buffer_452
  assign _4RB_FS = and_97_out ? 2'b01 : 2'bz;  // Controlled_Buffer controlled_buffer_453
  assign controlled_buffer_454_out = and_97_out ? out_1[10:8] : 3'bz;  // Controlled_Buffer controlled_buffer_454
  assign _4RB_FS = and_97_out ? 2'b01 : 2'bz;  // Controlled_Buffer controlled_buffer_455
  and and_98 (and_98_out, not_51_out, D13_LSR, T3, not_56_out);
  assign OutASel = and_98_out ? out_1[6:5] : 2'bz;  // Controlled_Buffer controlled_buffer_456
  assign MuxCSel = and_98_out ? 1'b1 : 1'bz;  // Controlled_Buffer controlled_buffer_457
  assign ALUFS = and_98_out ? 4'b1011 : 4'bz;  // Controlled_Buffer controlled_buffer_458
  assign MuxASel = and_98_out ? 2'b11 : 2'bz;  // Controlled_Buffer controlled_buffer_459
  assign controlled_buffer_460_out = and_98_out ? out_1[10:8] : 3'bz;  // Controlled_Buffer controlled_buffer_460
  Decoder #(.select(3)) decoder_43 (
    .out0(_4RB_RS[0]), .out1(_4RB_RS[1]), .out2(_4RB_RS[2]), .out3(_4RB_RS[3]),
    .sel(controlled_buffer_460_out), .en(and_98_out));  // open: out4, out5, out6, out7
  assign _4RB_FS = and_98_out ? 2'b01 : 2'bz;  // Controlled_Buffer controlled_buffer_461
  not not_54 (not_54_out, out_1[10]);
  Decoder #(.select(3)) decoder_44 (
    .out0(_4RB_RS[0]), .out1(_4RB_RS[1]), .out2(_4RB_RS[2]), .out3(_4RB_RS[3]),
    .sel(controlled_buffer_448_out), .en(and_96_out));  // open: out4, out5, out6, out7
  not not_55 (not_55_out, out_1[10]);
  outcdecoder outcdecoder_26 (.in_1(controlled_buffer_450_out), .out_2(OutCSel));
  Decoder #(.select(3)) decoder_45 (
    .out0(_4RB_RS[0]), .out1(_4RB_RS[1]), .out2(_4RB_RS[2]), .out3(_4RB_RS[3]),
    .sel(controlled_buffer_454_out), .en(and_97_out));  // open: out4, out5, out6, out7
  not not_56 (not_56_out, out_1[10]);
  and and_99 (and_99_out, out_1[7], D13_LSR, T4, not_62_out);
  not not_57 (not_57_out, out_1[10]);
  and and_100 (and_100_out, D9_AND, T4, not_57_out, not_61_out);
  assign OutDSel = and_100_out ? 2'b10 : 2'bz;  // Controlled_Buffer controlled_buffer_462
  assign MEM_SEL = and_100_out ? 1'b1 : 1'bz;  // Controlled_Buffer controlled_buffer_463
  assign MEM_LD = and_100_out ? 1'b1 : 1'bz;  // Controlled_Buffer controlled_buffer_464
  assign MuxASel = and_100_out ? 2'b01 : 2'bz;  // Controlled_Buffer controlled_buffer_465
  assign controlled_buffer_466_out = and_100_out ? out_1[9:8] : 2'bz;  // Controlled_Buffer controlled_buffer_466
  Decoder #(.select(2)) decoder_46 (
    .out0(_4RB_RS[0]), .out1(_4RB_RS[1]), .out2(_4RB_RS[2]), .out3(_4RB_RS[3]),
    .sel(controlled_buffer_466_out), .en(and_100_out));
  assign _4RB_FS = and_100_out ? 2'b01 : 2'bz;  // Controlled_Buffer controlled_buffer_467
  not not_58 (not_58_out, and_93_out);
  not not_59 (not_59_out, out_1[10]);
  and and_101 (and_101_out, D10_OR, T4, not_59_out, not_58_out);
  assign OutDSel = and_101_out ? 2'b10 : 2'bz;  // Controlled_Buffer controlled_buffer_468
  assign MEM_SEL = and_101_out ? 1'b1 : 1'bz;  // Controlled_Buffer controlled_buffer_469
  assign MEM_LD = and_101_out ? 1'b1 : 1'bz;  // Controlled_Buffer controlled_buffer_470
  assign MuxASel = and_101_out ? 2'b01 : 2'bz;  // Controlled_Buffer controlled_buffer_471
  assign controlled_buffer_472_out = and_101_out ? out_1[9:8] : 2'bz;  // Controlled_Buffer controlled_buffer_472
  Decoder #(.select(2)) decoder_47 (
    .out0(_4RB_RS[0]), .out1(_4RB_RS[1]), .out2(_4RB_RS[2]), .out3(_4RB_RS[3]),
    .sel(controlled_buffer_472_out), .en(and_101_out));
  assign _4RB_FS = and_101_out ? 2'b01 : 2'bz;  // Controlled_Buffer controlled_buffer_473
  not not_60 (not_60_out, out_1[7]);
  assign OutASel = and_99_out ? out_1[9:8] : 2'bz;  // Controlled_Buffer controlled_buffer_474
  assign MuxCSel = and_99_out ? 1'b1 : 1'bz;  // Controlled_Buffer controlled_buffer_475
  assign ALUFS = and_99_out ? 4'b1011 : 4'bz;  // Controlled_Buffer controlled_buffer_476
  assign MuxASel = and_99_out ? 2'b11 : 2'bz;  // Controlled_Buffer controlled_buffer_477
  Decoder #(.select(3)) decoder_48 (
    .out0(_4RB_RS[0]), .out1(_4RB_RS[1]), .out2(_4RB_RS[2]), .out3(_4RB_RS[3]),
    .sel(controlled_buffer_478_out), .en(and_99_out));  // open: out4, out5, out6, out7
  assign controlled_buffer_478_out = and_99_out ? out_1[10:8] : 3'bz;  // Controlled_Buffer controlled_buffer_478
  assign _4RB_FS = and_99_out ? 2'b01 : 2'bz;  // Controlled_Buffer controlled_buffer_479
  not not_61 (not_61_out, and_94_out);
  not not_62 (not_62_out, out_1[10]);
  and and_102 (and_102_out, D10_OR, T5, not_65_out);
  assign SCR = and_102_out ? 1'b1 : 1'bz;  // Controlled_Buffer controlled_buffer_480
  and and_103 (and_103_out, not_60_out, D7_DEC, T4, not_66_out);
  assign _4RB_FS = and_103_out ? 2'b11 : 2'bz;  // Controlled_Buffer controlled_buffer_481
  assign controlled_buffer_482_out = and_103_out ? out_1[10:8] : 3'bz;  // Controlled_Buffer controlled_buffer_482
  Decoder #(.select(3)) decoder_49 (
    .out0(_4RB_RS[0]), .out1(_4RB_RS[1]), .out2(_4RB_RS[2]), .out3(_4RB_RS[3]),
    .sel(controlled_buffer_482_out), .en(and_103_out));  // open: out4, out5, out6, out7
  and and_104 (and_104_out, out_1[7], D7_DEC, T4, not_67_out);
  assign _4RB_FS = and_104_out ? 2'b11 : 2'bz;  // Controlled_Buffer controlled_buffer_483
  Decoder #(.select(3)) decoder_50 (
    .out0(_4RB_RS[0]), .out1(_4RB_RS[1]), .out2(_4RB_RS[2]), .out3(_4RB_RS[3]),
    .sel(controlled_buffer_484_out), .en(and_104_out));  // open: out4, out5, out6, out7
  assign controlled_buffer_484_out = and_104_out ? out_1[10:8] : 3'bz;  // Controlled_Buffer controlled_buffer_484
  not not_63 (not_63_out, out_1[7]);
  not not_64 (not_64_out, out_1[10]);
  and and_105 (and_105_out, D9_AND, T5, not_64_out);
  assign SCR = and_105_out ? 1'b1 : 1'bz;  // Controlled_Buffer controlled_buffer_485
  not not_65 (not_65_out, out_1[10]);
  not not_66 (not_66_out, out_1[10]);
  not not_67 (not_67_out, out_1[10]);
  and and_106 (and_106_out, out_1[7], D13_LSR, T3, out_1[10]);
  assign controlled_buffer_486_out = and_106_out ? out_1[6:5] : 2'bz;  // Controlled_Buffer controlled_buffer_486
  outcdecoder outcdecoder_27 (.in_1(controlled_buffer_486_out), .out_2(OutCSel));
  assign MuxASel = and_106_out ? 2'b10 : 2'bz;  // Controlled_Buffer controlled_buffer_487
  assign MuxCSel = and_106_out ? 1'b0 : 1'bz;  // Controlled_Buffer controlled_buffer_488
  assign ALUFS = and_106_out ? 4'b1011 : 4'bz;  // Controlled_Buffer controlled_buffer_489
  assign MuxBSel = and_106_out ? 2'b11 : 2'bz;  // Controlled_Buffer controlled_buffer_490
  assign _3RB_FS = and_106_out ? 2'b01 : 2'bz;  // Controlled_Buffer controlled_buffer_491
  Decoder #(.select(2), .disabled(0)) decoder_51 (
    .out0(decoder_51_out0), .out1(decoder_51_out1), .out2(_3RB_RS[1]), .out3(_3RB_RS[2]),
    .sel(controlled_buffer_492_out), .en(and_106_out));
  assign controlled_buffer_492_out = and_106_out ? out_1[9:8] : 2'bz;  // Controlled_Buffer controlled_buffer_492
  or or_26 (_3RB_RS[0], decoder_51_out0, decoder_51_out1);
  and and_107 (and_107_out, not_63_out, D13_LSR, T3, out_1[10]);
  assign OutASel = and_107_out ? out_1[6:5] : 2'bz;  // Controlled_Buffer controlled_buffer_493
  assign MuxCSel = and_107_out ? 1'b1 : 1'bz;  // Controlled_Buffer controlled_buffer_494
  assign ALUFS = and_107_out ? 4'b1011 : 4'bz;  // Controlled_Buffer controlled_buffer_495
  assign MuxBSel = and_107_out ? 2'b11 : 2'bz;  // Controlled_Buffer controlled_buffer_496
  Decoder #(.select(2), .disabled(0)) decoder_52 (
    .out0(decoder_52_out0), .out1(decoder_52_out1), .out2(_3RB_RS[1]), .out3(_3RB_RS[2]),
    .sel(controlled_buffer_497_out), .en(and_107_out));
  assign controlled_buffer_497_out = and_107_out ? out_1[9:8] : 2'bz;  // Controlled_Buffer controlled_buffer_497
  or or_27 (_3RB_RS[0], decoder_52_out0, decoder_52_out1);
  assign _3RB_FS = and_107_out ? 2'b01 : 2'bz;  // Controlled_Buffer controlled_buffer_498
  not not_68 (not_68_out, out_1[7]);
  and and_108 (and_108_out, out_1[7], D7_DEC, T3, out_1[10]);
  assign controlled_buffer_499_out = and_108_out ? out_1[6:5] : 2'bz;  // Controlled_Buffer controlled_buffer_499
  assign MuxASel = and_108_out ? 2'b10 : 2'bz;  // Controlled_Buffer controlled_buffer_500
  assign MuxCSel = and_108_out ? 1'b0 : 1'bz;  // Controlled_Buffer controlled_buffer_501
  assign ALUFS = and_108_out ? 4'b0000 : 4'bz;  // Controlled_Buffer controlled_buffer_502
  assign MuxBSel = and_108_out ? 2'b11 : 2'bz;  // Controlled_Buffer controlled_buffer_503
  assign _3RB_FS = and_108_out ? 2'b01 : 2'bz;  // Controlled_Buffer controlled_buffer_504
  assign controlled_buffer_505_out = and_108_out ? out_1[9:8] : 2'bz;  // Controlled_Buffer controlled_buffer_505
  and and_109 (and_109_out, not_68_out, D7_DEC, T3, out_1[10]);
  assign OutASel = and_109_out ? out_1[6:5] : 2'bz;  // Controlled_Buffer controlled_buffer_506
  assign MuxCSel = and_109_out ? 1'b1 : 1'bz;  // Controlled_Buffer controlled_buffer_507
  assign ALUFS = and_109_out ? 4'b0000 : 4'bz;  // Controlled_Buffer controlled_buffer_508
  assign MuxBSel = and_109_out ? 2'b11 : 2'bz;  // Controlled_Buffer controlled_buffer_509
  assign controlled_buffer_510_out = and_109_out ? out_1[9:8] : 2'bz;  // Controlled_Buffer controlled_buffer_510
  assign _3RB_FS = and_109_out ? 2'b01 : 2'bz;  // Controlled_Buffer controlled_buffer_511
  not not_69 (not_69_out, out_1[7]);
  outcdecoder outcdecoder_28 (.in_1(controlled_buffer_499_out), .out_2(OutCSel));
  Decoder #(.select(2), .disabled(0)) decoder_53 (
    .out0(decoder_53_out0), .out1(decoder_53_out1), .out2(_3RB_RS[1]), .out3(_3RB_RS[2]),
    .sel(controlled_buffer_505_out), .en(and_108_out));
  or or_28 (_3RB_RS[0], decoder_53_out0, decoder_53_out1);
  Decoder #(.select(2), .disabled(0)) decoder_54 (
    .out0(decoder_54_out0), .out1(decoder_54_out1), .out2(_3RB_RS[1]), .out3(_3RB_RS[2]),
    .sel(controlled_buffer_510_out), .en(and_109_out));
  or or_29 (_3RB_RS[0], decoder_54_out0, decoder_54_out1);
  and and_110 (and_110_out, out_1[7], out_1[10]);
  or or_30 (or_30_out, not_69_out, and_110_out);
  and and_111 (and_111_out, or_30_out, D13_LSR, T4);
  not not_70 (not_70_out, out_1[7]);
  assign SCR = and_111_out ? 1'b1 : 1'bz;  // Controlled_Buffer controlled_buffer_512
  and and_112 (and_112_out, out_1[7], D13_LSR, T5, not_71_out);
  assign SCR = and_112_out ? 1'b1 : 1'bz;  // Controlled_Buffer controlled_buffer_513
  not not_71 (not_71_out, out_1[10]);
  and and_113 (and_113_out, out_1[7], D7_DEC, T4, out_1[10]);
  assign _3RB_FS = and_113_out ? 2'b11 : 2'bz;  // Controlled_Buffer controlled_buffer_514
  assign controlled_buffer_515_out = and_113_out ? out_1[9:8] : 2'bz;  // Controlled_Buffer controlled_buffer_515
  Decoder #(.select(2), .disabled(0)) decoder_55 (
    .out0(decoder_55_out0), .out1(decoder_55_out1), .out2(_3RB_RS[1]), .out3(_3RB_RS[2]),
    .sel(controlled_buffer_515_out), .en(and_113_out));
  or or_31 (_3RB_RS[0], decoder_55_out0, decoder_55_out1);
  and and_114 (and_114_out, not_70_out, D7_DEC, T4, out_1[10]);
  assign _3RB_FS = and_114_out ? 2'b11 : 2'bz;  // Controlled_Buffer controlled_buffer_516
  assign controlled_buffer_517_out = and_114_out ? out_1[9:8] : 2'bz;  // Controlled_Buffer controlled_buffer_517
  Decoder #(.select(2), .disabled(0)) decoder_56 (
    .out0(decoder_56_out0), .out1(decoder_56_out1), .out2(_3RB_RS[1]), .out3(_3RB_RS[2]),
    .sel(controlled_buffer_517_out), .en(and_114_out));
  or or_32 (_3RB_RS[0], decoder_56_out0, decoder_56_out1);
  assign MEM_SEL = D11_NOT ? 1'b0 : 1'bz;  // Controlled_Buffer controlled_buffer_518
  assign MEM_LD = D11_NOT ? 1'b0 : 1'bz;  // Controlled_Buffer controlled_buffer_519
  assign MEM_STR = D11_NOT ? 1'b0 : 1'bz;  // Controlled_Buffer controlled_buffer_520
  assign MEM_CLR = D11_NOT ? 1'b0 : 1'bz;  // Controlled_Buffer controlled_buffer_521
  and and_115 (and_115_out, D7_DEC, T6);
  assign SCR = and_115_out ? 1'b1 : 1'bz;  // Controlled_Buffer controlled_buffer_522
  not not_72 (not_72_out, out_1[10]);
  and and_116 (and_116_out, D7_DEC, T5, not_72_out);
  assign _4RB_RS = and_116_out ? 4'b0000 : 4'bz;  // Controlled_Buffer controlled_buffer_523
  assign OutASel = and_116_out ? out_1[9:8] : 2'bz;  // Controlled_Buffer controlled_buffer_524
  assign MuxCSel = and_116_out ? 1'b1 : 1'bz;  // Controlled_Buffer controlled_buffer_525
  and and_117 (and_117_out, D7_DEC, T5, out_1[10]);
  assign _3RB_RS = and_117_out ? 4'b0000 : 4'bz;  // Controlled_Buffer controlled_buffer_526
  outcdecoder outcdecoder_29 (.in_1(controlled_buffer_527_out), .out_2(OutCSel));
  assign controlled_buffer_527_out = and_117_out ? out_1[9:8] : 2'bz;  // Controlled_Buffer controlled_buffer_527
  assign MuxASel = and_117_out ? 2'b11 : 2'bz;  // Controlled_Buffer controlled_buffer_528
  assign _4RB_RS = and_117_out ? 4'b0000 : 4'bz;  // Controlled_Buffer controlled_buffer_529
  assign MuxCSel = and_117_out ? 1'b0 : 1'bz;  // Controlled_Buffer controlled_buffer_530
  and and_118 (and_118_out, out_1[7], D11_NOT, T3, not_74_out);
  assign controlled_buffer_531_out = and_118_out ? out_1[6:5] : 2'bz;  // Controlled_Buffer controlled_buffer_531
  assign MuxASel = and_118_out ? 2'b10 : 2'bz;  // Controlled_Buffer controlled_buffer_532
  assign MuxCSel = and_118_out ? 1'b0 : 1'bz;  // Controlled_Buffer controlled_buffer_533
  assign _4RB_FS = and_118_out ? 2'b01 : 2'bz;  // Controlled_Buffer controlled_buffer_534
  assign controlled_buffer_535_out = and_118_out ? out_1[10:8] : 3'bz;  // Controlled_Buffer controlled_buffer_535
  assign _4RB_FS = and_118_out ? 2'b01 : 2'bz;  // Controlled_Buffer controlled_buffer_536
  not not_73 (not_73_out, out_1[7]);
  not not_74 (not_74_out, out_1[10]);
  outcdecoder outcdecoder_30 (.in_1(controlled_buffer_531_out), .out_2(OutCSel));
  Decoder #(.select(3)) decoder_57 (
    .out0(_4RB_RS[0]), .out1(_4RB_RS[1]), .out2(_4RB_RS[2]), .out3(_4RB_RS[3]),
    .sel(controlled_buffer_535_out), .en(and_118_out));  // open: out4, out5, out6, out7
  and and_119 (and_119_out, not_73_out, D11_NOT, T3, not_75_out);
  assign OutASel = and_119_out ? out_1[6:5] : 2'bz;  // Controlled_Buffer controlled_buffer_537
  assign MuxCSel = and_119_out ? 1'b1 : 1'bz;  // Controlled_Buffer controlled_buffer_538
  assign ALUFS = and_119_out ? 4'b0010 : 4'bz;  // Controlled_Buffer controlled_buffer_539
  assign MuxASel = and_119_out ? 2'b11 : 2'bz;  // Controlled_Buffer controlled_buffer_540
  assign controlled_buffer_541_out = and_119_out ? out_1[10:8] : 3'bz;  // Controlled_Buffer controlled_buffer_541
  assign _4RB_FS = and_119_out ? 2'b01 : 2'bz;  // Controlled_Buffer controlled_buffer_542
  not not_75 (not_75_out, out_1[10]);
  Decoder #(.select(3)) decoder_58 (
    .out0(_4RB_RS[0]), .out1(_4RB_RS[1]), .out2(_4RB_RS[2]), .out3(_4RB_RS[3]),
    .sel(controlled_buffer_541_out), .en(and_119_out));  // open: out4, out5, out6, out7
  and and_120 (and_120_out, out_1[7], D11_NOT, T4, not_76_out);
  assign OutASel = and_120_out ? out_1[9:8] : 2'bz;  // Controlled_Buffer controlled_buffer_543
  assign MuxCSel = and_120_out ? 1'b1 : 1'bz;  // Controlled_Buffer controlled_buffer_544
  assign ALUFS = and_120_out ? 4'b0010 : 4'bz;  // Controlled_Buffer controlled_buffer_545
  assign MuxASel = and_120_out ? 2'b11 : 2'bz;  // Controlled_Buffer controlled_buffer_546
  Decoder #(.select(3)) decoder_59 (
    .out0(_4RB_RS[0]), .out1(_4RB_RS[1]), .out2(_4RB_RS[2]), .out3(_4RB_RS[3]),
    .sel(controlled_buffer_547_out), .en(and_120_out));  // open: out4, out5, out6, out7
  assign controlled_buffer_547_out = and_120_out ? out_1[10:8] : 3'bz;  // Controlled_Buffer controlled_buffer_547
  assign _4RB_FS = and_120_out ? 2'b01 : 2'bz;  // Controlled_Buffer controlled_buffer_548
  not not_76 (not_76_out, out_1[10]);
  not not_77 (not_77_out, out_1[7]);
  and and_121 (and_121_out, out_1[7], D11_NOT, T3, out_1[10]);
  assign controlled_buffer_549_out = and_121_out ? out_1[6:5] : 2'bz;  // Controlled_Buffer controlled_buffer_549
  outcdecoder outcdecoder_31 (.in_1(controlled_buffer_549_out), .out_2(OutCSel));
  assign MuxASel = and_121_out ? 2'b10 : 2'bz;  // Controlled_Buffer controlled_buffer_550
  assign MuxCSel = and_121_out ? 1'b0 : 1'bz;  // Controlled_Buffer controlled_buffer_551
  assign ALUFS = and_121_out ? 4'b0010 : 4'bz;  // Controlled_Buffer controlled_buffer_552
  assign MuxBSel = and_121_out ? 2'b11 : 2'bz;  // Controlled_Buffer controlled_buffer_553
  assign _3RB_FS = and_121_out ? 2'b01 : 2'bz;  // Controlled_Buffer controlled_buffer_554
  Decoder #(.select(2), .disabled(0)) decoder_60 (
    .out0(decoder_60_out0), .out1(decoder_60_out1), .out2(_3RB_RS[1]), .out3(_3RB_RS[2]),
    .sel(controlled_buffer_555_out), .en(and_121_out));
  assign controlled_buffer_555_out = and_121_out ? out_1[9:8] : 2'bz;  // Controlled_Buffer controlled_buffer_555
  or or_33 (_3RB_RS[0], decoder_60_out0, decoder_60_out1);
  and and_122 (and_122_out, not_77_out, D11_NOT, T3, out_1[10]);
  assign OutASel = and_122_out ? out_1[6:5] : 2'bz;  // Controlled_Buffer controlled_buffer_556
  assign MuxCSel = and_122_out ? 1'b1 : 1'bz;  // Controlled_Buffer controlled_buffer_557
  assign ALUFS = and_122_out ? 4'b0010 : 4'bz;  // Controlled_Buffer controlled_buffer_558
  assign MuxBSel = and_122_out ? 2'b11 : 2'bz;  // Controlled_Buffer controlled_buffer_559
  assign controlled_buffer_560_out = and_122_out ? out_1[9:8] : 2'bz;  // Controlled_Buffer controlled_buffer_560
  assign _3RB_FS = and_122_out ? 2'b01 : 2'bz;  // Controlled_Buffer controlled_buffer_561
  Decoder #(.select(2), .disabled(0)) decoder_61 (
    .out0(decoder_61_out0), .out1(decoder_61_out1), .out2(_3RB_RS[1]), .out3(_3RB_RS[2]),
    .sel(controlled_buffer_560_out), .en(and_122_out));
  or or_34 (_3RB_RS[0], decoder_61_out0, decoder_61_out1);
  not not_78 (not_78_out, out_1[7]);
  or or_35 (or_35_out, not_78_out, and_123_out);
  and and_123 (and_123_out, out_1[7], out_1[10]);
  and and_124 (and_124_out, or_35_out, D11_NOT, T4);
  assign SCR = and_124_out ? 1'b1 : 1'bz;  // Controlled_Buffer controlled_buffer_562
  and and_125 (and_125_out, out_1[7], D11_NOT, T5, not_79_out);
  assign SCR = and_125_out ? 1'b1 : 1'bz;  // Controlled_Buffer controlled_buffer_563
  not not_79 (not_79_out, out_1[10]);

  // Other names for the same wires on the sheet: AdrMOD = out_1[8]; DESTREG[2:0] = out_1[10:8]; INSTR[15:0] = out_1;
  //   REGSEL[1:0] = out_1[10:9]; ADDRESS[7:0] = out_1[7:0]; SRCREG2[2:0] = out_1[4:2]; SRCREG1[2:0] = out_1[7:5];
  //   OPCODE[4:0] = out_1[15:11]

  // Notes on the sheet:
  //   BRA
  //   SUB (DEST IN 3RB)
  //   MOV
  //   ADD (DEST IN 3RB)
  //   LD
  //   BEQ & BNE
  //   CALL
  //   ADD (DEST IN 4RB)
  //   SUB (DEST IN 4RB)
  //   RET
  //   ST
  //   FROM 3
  //   PSH
  //   FROM 4
  //   PUL
  //   TO 3
  //   TO 4
  //   OR (DEST IN 3RB)
  //   AND (DEST IN 3RB)
  //   4RB TO 4RB
  //   3RB TO 4RB
  //   4RB TO 4RB
  //   3RB TO 4RB
  //   INC
  //   LSL
  //   3RB TO 3RB
  //   4RB TO 3RB
  //   3RB TO 3RB
  //   4RB TO 3RB
  //   AND (DEST IN 4RB)
  //   OR (DEST IN 4RB)
  //   IF NOT 3RB to 4RB
  //   IF 3RB to 4RB
  //   Sending to ALU for Flags
  //   4RB TO 4RB
  //   3RB TO 4RB
  //   4RB TO 4RB
  //   3RB TO 4RB
  //   LSR
  //   DEC
  //   3RB TO 3RB
  //   4RB TO 3RB
  //   3RB TO 3RB
  //   4RB TO 3RB
  //   IF NOT 3RB to 4RB
  //   IF 3RB to 4RB
  //   Sending to ALU for Flags
  //   4RB TO 4RB
  //   3RB TO 4RB
  //   NOT
  //   3RB TO 3RB
  //   4RB TO 3RB
  //   IF NOT 3RB to 4RB
  //   IF 3RB to 4RB
endmodule

module counter (
  input  in_1,
  output out_2,
  output out_3,
  output out_4,
  output out_5,
  output out_6,
  output out_7,
  output out_8,
  output out_9
);

  wire clock_1_out;
  wire [2:0] counter_1_q;

  Counter #(.width(3), .max('h7)) counter_1 (
    .Q(counter_1_q), .clk(clock_1_out), .clr(in_1));  // open: load, D, count, carry
  Clock clock_1 (.out(clock_1_out));
  Decoder #(.select(3), .enable("false")) decoder_1 (
    .out0(out_2), .out1(out_3), .out2(out_4), .out3(out_5), .out4(out_6), .out5(out_7), .out6(out_8),
    .out7(out_9), .sel(counter_1_q));
endmodule

module outcdecoder (
  input  [1:0] in_1,
  output [1:0] out_2
);

  Subtractor #(.width(2)) subtractor_1 (.a(in_1), .b(2'b01), .out(out_2));  // open: bin, bout
endmodule
