// Logisim project part2.circ as structural Verilog: 1 circuit, main circuit main
module main (
  input  MuxCSel,
  input  [3:0] FunSel,
  input  [1:0] OutASel,
  input  [1:0] OutBSel,
  input  [1:0] FunSel_2,
  input  [3:0] RegSel,
  input  [1:0] MuxASel,
  input  [1:0] MuxBSel,
  input  in_9,
  input  in_10,
  input  in_11,
  input  in_12,
  input  [1:0] OutCSel,
  input  [1:0] OutDSel,
  input  [1:0] FunSel_3,
  input  [3:0] RegSel_2,
  input  L_H,
  input  Enable,
  input  [1:0] FunSel_4,
  output [7:0] out_20,
  output [3:0] out_21
);

  wire clock_1_out;
  wire [3:0] register_1_q;
  wire [7:0] main_1_out_6, multiplexer_1_out, multiplexer_2_out, multiplexer_3_out, n3_register_bank_1_out_7,
       n3_register_bank_1_out_8, n4_register_bank_1_out_7, n4_register_bank_1_out_8, ram_1_data;
  wire [15:8] main_1_out_6_2;

  Clock clock_1 (.out(clock_1_out));
  Multiplexer #(.select(2), .width(8), .enable("false")) multiplexer_1 (
    .in0(main_1_out_6), .in1(ram_1_data), .in2(n3_register_bank_1_out_7), .in3(out_20),
    .out(multiplexer_1_out), .sel(MuxASel));
  _4_register_bank u_4_register_bank_1 (
    .RegSel(RegSel), .CLK(clock_1_out), .in_3(multiplexer_1_out), .Funsel(FunSel_2), .OutCSel(OutASel),
    .OutDSel(OutBSel), .out_7(n4_register_bank_1_out_7), .out_8(n4_register_bank_1_out_8));
  Multiplexer #(.select(2), .width(8), .enable("false")) multiplexer_2 (
    .in1(main_1_out_6), .in2(ram_1_data), .in3(out_20), .out(multiplexer_2_out), .sel(MuxBSel));  // open: in0
  _2c_main main_1 (
    .in_1(ram_1_data), .out_6({main_1_out_6_2, main_1_out_6}), .ENABLE(Enable), .CLK(clock_1_out),
    .Function_Selector(FunSel_4), .L_H(L_H));
  Multiplexer #(.width(8), .enable("false")) multiplexer_3 (
    .in0(multiplexer_1_out), .in1(n4_register_bank_1_out_7), .out(multiplexer_3_out), .sel(MuxCSel));
  alu2_main main_2 (
    .Out(out_20), .FunSel(FunSel), .A(multiplexer_3_out), .B(n4_register_bank_1_out_8),
    .in_4(register_1_q[2]), .out_6(out_21));
  _3_register_bank u_3_register_bank_1 (
    .RegSel(RegSel_2), .CLK(clock_1_out), .in_3(multiplexer_2_out), .Funsel(FunSel_3), .OutCSel(OutCSel),
    .OutDSel(OutDSel), .out_7(n3_register_bank_1_out_7), .out_8(n3_register_bank_1_out_8));
  Register #(.width(4)) register_1 (.D(out_21), .en(1'b1), .Q(register_1_q), .clk(clock_1_out));  // open: clr
  RAM #(.bus("separate")) ram_1 (
    .addr(out_20), .din(n3_register_bank_1_out_8), .data(ram_1_data), .str(in_9), .sel(in_10),
    .clk(clock_1_out), .ld(in_11), .clr(in_12));

  // Notes on the sheet:
  //   A
  //   B
  //   C
endmodule
